// Digital circuit CPU.dig as structural Verilog
module CPU (
);

  wire and_1_out, and_2_out, or_1_out, or_2_out, u_CheckEqual_isequal, u_Control_brancheq,
       u_Control_branchneq, u_Control_immsrc, u_Control_jal, u_Control_jalr, u_EX_MEM_memread,
       u_EX_MEM_memwrite, u_EX_MEM_regwrite_out, u_HazardUnit_stallpipeline, u_ID_EX_alusrcb,
       u_ID_EX_memread, u_JALR_2ndCycle_FF_jalr_2ndcycle, u_MEM_WB_memtoreg, u_MEM_WB_regwrite;
  wire [1:0] u_Control_memsignals, u_Control_wbsignals, u_EX_MEM_wbsignals_out, u_ForwardingUnit_forwarda,
       u_ForwardingUnit_forwardb, u_ID_EX_aluop, u_ID_EX_alusrca, u_ID_EX_memsignals_out,
       u_ID_EX_wbsignals_out, u_Mux_ControlSignals_memsignals_out, u_Mux_ControlSignals_wbsignals_out;
  wire [2:0] u_ID_EX_func3_out, u_IF_ID_func3;
  wire [3:0] u_ALUControl_aluctl;
  wire [4:0] u_Control_exsignals, u_EX_MEM_rd_out, u_ID_EX_rd_out, u_ID_EX_rs1_out, u_ID_EX_rs2_out,
       u_IF_ID_rd, u_IF_ID_rs1, u_IF_ID_rs2, u_MEM_WB_rd_out, u_Mux_ControlSignals_exsignals_out;
  wire [6:0] u_ID_EX_func7_out, u_IF_ID_func7;
  wire [15:0] u_PC_pc_out_16b;
  wire [31:0] InstMem_d, u_ALU_aluout, u_ALUSrcA_a, u_ALUSrcB_b, u_EX_MEM_aluoutput_out,
       u_EX_MEM_rs2_data_out, u_FowardingA_a, u_FowardingB_b, u_ID_EX_immediate_out, u_ID_EX_pc_out,
       u_ID_EX_rs1_data_out, u_ID_EX_rs2_data_out, u_IF_ID_inst_out, u_IF_ID_pc_out, u_ImmGen_immediate,
       u_MEM_WB_aluoutput_out, u_MEM_WB_datafrommem_out, u_MemToReg_dataout, u_PC_pc_out,
       u_PCPlusImm_next_pc, u_PCPlusOne_next_pc, u_PCSrc_nextpc, u_RAM_dout, u_RegisterFile_da,
       u_RegisterFile_db;

  or or_1 (or_1_out, and_1_out, and_2_out, u_Control_jal);
  PCSrc #(.applicationType("GHDL")) u_PCSrc (
    .PCplus4(u_PCPlusOne_next_pc), .ID_result(u_PCPlusImm_next_pc), .EX_result(u_ALU_aluout),
    .S1(u_JALR_2ndCycle_FF_jalr_2ndcycle), .S2(or_1_out), .NextPC(u_PCSrc_nextpc));
  PCPlusOne #(.applicationType("GHDL")) u_PCPlusOne (.PC(u_PC_pc_out), .Next_PC(u_PCPlusOne_next_pc));
  PC #(.applicationType("GHDL")) u_PC (
    .PC_in(u_PCSrc_nextpc), .PC_out(u_PC_pc_out), .PC_out_16b(u_PC_pc_out_16b));  // open: rst, clk, PC_WRITE
  or or_2 (or_2_out, u_JALR_2ndCycle_FF_jalr_2ndcycle, or_1_out);
  ROM #(.AddrBits(16), .Bits(32)) InstMem (.A(u_PC_pc_out_16b), .D(InstMem_d));  // open: sel
  IF_ID #(.applicationType("GHDL")) u_IF_ID (
    .IF_ID_WRITE(u_Control_jalr), .IF_ID_flush(or_2_out), .PC_in(u_PC_pc_out), .inst_in(InstMem_d),
    .PC_out(u_IF_ID_pc_out), .inst_out(u_IF_ID_inst_out), .rd(u_IF_ID_rd), .rs1(u_IF_ID_rs1),
    .rs2(u_IF_ID_rs2), .func3(u_IF_ID_func3), .func7(u_IF_ID_func7));  // open: rst, clk
  JALR_2ndCycle_FF #(.applicationType("GHDL")) u_JALR_2ndCycle_FF (
    .JALR_in(u_Control_jalr), .JALR_2ndCycle(u_JALR_2ndCycle_FF_jalr_2ndcycle));  // open: clk, rst
  Control #(.applicationType("GHDL")) u_Control (
    .JALR_2ndCycle(u_JALR_2ndCycle_FF_jalr_2ndcycle), .Instr(u_IF_ID_inst_out), .JALR(u_Control_jalr),
    .JAL(u_Control_jal), .BranchEQ(u_Control_brancheq), .BranchNEQ(u_Control_branchneq),
    .EXSignals(u_Control_exsignals), .MEMSignals(u_Control_memsignals), .WBSignals(u_Control_wbsignals),
    .ImmSrc(u_Control_immsrc));
  HazardUnit #(.applicationType("GHDL")) u_HazardUnit (
    .ID_EX_MemRead(u_ID_EX_memread), .ID_EX_RegisterRd(u_ID_EX_rd_out), .IF_ID_RegisterRs1(u_IF_ID_rs1),
    .IF_ID_RegisterRs2(u_IF_ID_rs2), .StallPipeline(u_HazardUnit_stallpipeline));
  PCPlusImm #(.applicationType("GHDL")) u_PCPlusImm (
    .PC(u_IF_ID_pc_out), .IMM(u_ImmGen_immediate), .Next_PC(u_PCPlusImm_next_pc));
  RegisterFile #(.applicationType("GHDL")) u_RegisterFile (
    .Din(u_MemToReg_dataout), .we(u_MEM_WB_regwrite), .Rw(u_MEM_WB_rd_out), .Ra(u_IF_ID_rs1),
    .Rb(u_IF_ID_rs2), .Da(u_RegisterFile_da), .Db(u_RegisterFile_db));  // open: C, rst
  ImmGen #(.applicationType("GHDL")) u_ImmGen (.Instruction(u_IF_ID_inst_out), .Immediate(u_ImmGen_immediate));
  Mux_ControlSignals #(.applicationType("GHDL")) u_Mux_ControlSignals (
    .stall(u_HazardUnit_stallpipeline), .EXSignals_in(u_Control_exsignals),
    .MEMSignals_in(u_Control_memsignals), .WBSignals_in(u_Control_wbsignals),
    .EXSignals_out(u_Mux_ControlSignals_exsignals_out), .MEMSignals_out(u_Mux_ControlSignals_memsignals_out),
    .WBSignals_out(u_Mux_ControlSignals_wbsignals_out));
  CheckEqual #(.applicationType("GHDL")) u_CheckEqual (
    .Rs1(u_RegisterFile_da), .Rs2(u_RegisterFile_db), .IsEqual(u_CheckEqual_isequal));
  and and_1 (and_1_out, u_Control_brancheq, u_CheckEqual_isequal);
  Mux_ImmSrc #(.applicationType("GHDL")) u_Mux_ImmSrc (
    .SEL(u_Control_immsrc), .imm_in(u_ImmGen_immediate));  // open: imm_out
  and and_2 (and_2_out, ~u_CheckEqual_isequal, u_Control_branchneq);  // And
  ID_EX #(.applicationType("GHDL")) u_ID_EX (
    .EXSignals_in(u_Mux_ControlSignals_exsignals_out), .MEMSignals_in(u_Mux_ControlSignals_memsignals_out),
    .WBSignals_in(u_Mux_ControlSignals_wbsignals_out), .PC_in(u_IF_ID_pc_out),
    .rs1_data_in(u_RegisterFile_da), .rs2_data_in(u_RegisterFile_db), .rd_in(u_IF_ID_rd),
    .rs1_in(u_IF_ID_rs1), .rs2_in(u_IF_ID_rs2), .func3_in(u_IF_ID_func3), .func7_in(u_IF_ID_func7),
    .rs1_data_out(u_ID_EX_rs1_data_out), .rs2_data_out(u_ID_EX_rs2_data_out), .PC_out(u_ID_EX_pc_out),
    .immediate_out(u_ID_EX_immediate_out), .ALUSrcA(u_ID_EX_alusrca), .ALUSrcB(u_ID_EX_alusrcb),
    .func3_out(u_ID_EX_func3_out), .func7_out(u_ID_EX_func7_out), .ALUOp(u_ID_EX_aluop),
    .rs1_out(u_ID_EX_rs1_out), .rs2_out(u_ID_EX_rs2_out), .MemRead(u_ID_EX_memread), .rd_out(u_ID_EX_rd_out),
    .MEMSignals_out(u_ID_EX_memsignals_out), .WBSignals_out(u_ID_EX_wbsignals_out));  // open: rst, clk, immediate_in
  FowardingA #(.applicationType("GHDL")) u_FowardingA (
    .ID_EX(u_ID_EX_rs1_data_out), .EX_MEM(u_EX_MEM_aluoutput_out), .MEM_WB(u_MemToReg_dataout),
    .SEL(u_ForwardingUnit_forwarda), .A(u_FowardingA_a));
  FowardingB #(.applicationType("GHDL")) u_FowardingB (
    .ID_EX(u_ID_EX_rs2_data_out), .EX_MEM(u_EX_MEM_aluoutput_out), .MEM_WB(u_MemToReg_dataout),
    .SEL(u_ForwardingUnit_forwardb), .B(u_FowardingB_b));
  ALUControl #(.applicationType("GHDL")) u_ALUControl (
    .ALUOp(u_ID_EX_aluop), .Funct3(u_ID_EX_func3_out), .Funct7(u_ID_EX_func7_out),
    .ALUCtl(u_ALUControl_aluctl));
  ForwardingUnit #(.applicationType("GHDL")) u_ForwardingUnit (
    .ID_EX_RegisterRs1(u_ID_EX_rs1_out), .ID_EX_RegisterRs2(u_ID_EX_rs2_out),
    .EX_MEM_RegisterRd(u_EX_MEM_rd_out), .EX_MEM_RegWrite(u_EX_MEM_regwrite_out),
    .MEM_WB_RegisterRd(u_MEM_WB_rd_out), .MEM_WB_RegWrite(u_MEM_WB_regwrite),
    .ForwardA(u_ForwardingUnit_forwarda), .ForwardB(u_ForwardingUnit_forwardb));
  ALUSrcA #(.applicationType("GHDL")) u_ALUSrcA (
    .Rs1(u_FowardingA_a), .PC(u_ID_EX_pc_out), .SEL(u_ID_EX_alusrca), .A(u_ALUSrcA_a));
  ALUSrcB #(.applicationType("GHDL")) u_ALUSrcB (
    .Rs2(u_FowardingB_b), .imm(u_ID_EX_immediate_out), .SEL(u_ID_EX_alusrcb), .B(u_ALUSrcB_b));
  ALU #(.applicationType("GHDL")) u_ALU (
    .ALUctl(u_ALUControl_aluctl), .A(u_ALUSrcA_a), .B(u_ALUSrcB_b), .ALUOut(u_ALU_aluout));
  EX_MEM #(.applicationType("GHDL")) u_EX_MEM (
    .ALUoutput_in(u_ALU_aluout), .rs2_data_in(u_ALUSrcB_b), .rd_in(u_ID_EX_rd_out),
    .MEMSignals_in(u_ID_EX_memsignals_out), .WBSignals_in(u_ID_EX_wbsignals_out),
    .ALUoutput_out(u_EX_MEM_aluoutput_out), .rs2_data_out(u_EX_MEM_rs2_data_out), .MemRead(u_EX_MEM_memread),
    .MemWrite(u_EX_MEM_memwrite), .rd_out(u_EX_MEM_rd_out), .WBSignals_out(u_EX_MEM_wbsignals_out),
    .RegWrite_out(u_EX_MEM_regwrite_out));  // open: rst, clk
  RAM #(.applicationType("GHDL")) u_RAM (
    .Addr(u_EX_MEM_aluoutput_out), .Din(u_EX_MEM_rs2_data_out), .Read(u_EX_MEM_memread),
    .Write(u_EX_MEM_memwrite), .Dout(u_RAM_dout));  // open: clk
  MEM_WB #(.applicationType("GHDL")) u_MEM_WB (
    .DataFromMem_in(u_RAM_dout), .ALUoutput_in(u_EX_MEM_aluoutput_out), .rd_in(u_EX_MEM_rd_out),
    .WBSignals_in(u_EX_MEM_wbsignals_out), .rd_out(u_MEM_WB_rd_out),
    .DataFromMem_out(u_MEM_WB_datafrommem_out), .ALUoutput_out(u_MEM_WB_aluoutput_out),
    .MemToReg(u_MEM_WB_memtoreg), .RegWrite(u_MEM_WB_regwrite));  // open: rst, clk
  MemToReg #(.applicationType("GHDL")) u_MemToReg (
    .MemOutput(u_MEM_WB_datafrommem_out), .ALUOutput(u_MEM_WB_aluoutput_out), .SEL(u_MEM_WB_memtoreg),
    .DataOut(u_MemToReg_dataout));
endmodule

/* Code of PCSrc:
library IEEE;
use IEEE.STD_LOGIC_1164.ALL;

entity PCSrc is
    Port (
        PCplus4 	: in  std_logic_vector(31 downto 0); -- Entrada de dados 0
        ID_result  	: in  std_logic_vector(31 downto 0); -- Entrada de dados 1
        EX_result	: in  std_logic_vector(31 downto 0); -- Entrada de dados 2
        S1 		: in  std_logic; -- Linha de seleção
        S2 		: in  std_logic; -- Linha de seleção
        NextPC 		: out std_logic_vector(31 downto 0)  -- Saída de dados
    );
end PCSrc;

architecture Behavorial of PCSrc is
signal SEL : std_logic_vector(1 downto 0);
begin
SEL <= S1&S2;
    process(PCplus4, ID_result, EX_result, S1, S2)
    begin
        case SEL is
            when "00"   => NextPC <= PCplus4;
            when "01"   => NextPC <= ID_result;
            when "10"   => NextPC <= EX_result;
            when others => NextPC <= (others => '0'); -- valores incorretos
        end case;
    end process;

end Behavorial;
*/

/* Code of PCPlusOne:
library IEEE;
use IEEE.STD_LOGIC_1164.ALL;
use IEEE.NUMERIC_STD.ALL;

entity PCPlusOne is
    Port (
        PC        : in  STD_LOGIC_VECTOR(31 downto 0);
        Next_PC   : out  STD_LOGIC_VECTOR(31 downto 0)
    );
end PCPlusOne;

architecture Behavioral of PCPlusOne is
begin
	Next_PC <= std_logic_vector(unsigned(PC) + 1);
end Behavioral;
*/

/* Code of PC:
library IEEE;
use IEEE.STD_LOGIC_1164.ALL;

entity PC is
    Port ( 
	rst     	: in  STD_LOGIC; 
        clk		: in  STD_LOGIC;

        PC_in		: in  STD_LOGIC_VECTOR(31 downto 0);
	PC_WRITE	: in STD_LOGIC;
	PC_out		: out STD_LOGIC_VECTOR(31 downto 0);
	PC_out_16b	: out STD_LOGIC_VECTOR(15 downto 0)
    );
end PC;

architecture Behavioral of PC is

signal s_dado : STD_LOGIC_VECTOR(31 downto 0);

begin

process(clk,rst)
begin
	if rst = '1' then
		PC_out <= (others => '0');
        elsif rising_edge(clk) and PC_WRITE='0' then
		PC_out <= PC_in;
	end if;
end process;

PC_out_16b <= PC_out(15 downto 0);

end Behavioral;
*/

/* Code of IF_ID:
library IEEE;
use IEEE.STD_LOGIC_1164.ALL;

entity IF_ID is
    Port ( 
	rst     	: in  STD_LOGIC; 
        clk		: in  STD_LOGIC;

	IF_ID_WRITE	: in STD_LOGIC;
	IF_ID_flush	: in STD_LOGIC;
        PC_in		: in  STD_LOGIC_VECTOR(31 downto 0);
        inst_in		: in  STD_LOGIC_VECTOR(31 downto 0);

	PC_out		: out STD_LOGIC_VECTOR(31 downto 0);
	inst_out	: out STD_LOGIC_VECTOR(31 downto 0);
	rd		: out STD_LOGIC_VECTOR(4 downto 0);
        rs1		: out STD_LOGIC_VECTOR(4 downto 0);
        rs2		: out STD_LOGIC_VECTOR(4 downto 0);
	func3		: out STD_LOGIC_VECTOR(2 downto 0);
	func7		: out STD_LOGIC_VECTOR(6 downto 0)

    );
end IF_ID;

architecture Behavioral of IF_ID is

signal s_dado : STD_LOGIC_VECTOR(31 downto 0);

begin

process(clk,rst)
begin
	if rst = '1' then
		s_dado <= (others => '0');
        elsif rising_edge(clk) and IF_ID_WRITE='0' then
		if IF_ID_flush='1' then
			PC_out <= (others => '0');
			inst_out <= (others => '0');
		else
			PC_out <= PC_in;
            		inst_out <= inst_in;
		end if;
	end if;
end process;

rs1 <= inst_out(19 downto 15);
rs2 <= inst_out(24 downto 20);
rd <= inst_out(11 downto 7);
func3 <= inst_out(14 downto 12);
func7 <= inst_out(31 downto 25);

end Behavioral;
*/

/* Code of JALR_2ndCycle_FF:
library IEEE;
use IEEE.STD_LOGIC_1164.ALL;

entity JALR_2ndCycle_FF is
    Port (
        clk          : in  std_logic;
        rst          : in  std_logic;
        JALR_in      : in  std_logic;  -- sinal JALR do Control
        JALR_2ndCycle: out std_logic   -- sinal que indica o 2º ciclo
    );
end JALR_2ndCycle_FF;

architecture Behavioral of JALR_2ndCycle_FF is
    signal jalr_reg : std_logic := '0';
begin
    process(clk, rst)
    begin
        if rst = '1' then
            jalr_reg <= '0';
        elsif rising_edge(clk) then
            jalr_reg <= JALR_in;
        end if;
    end process;

    JALR_2ndCycle <= jalr_reg;
end Behavioral;
*/

/* Code of Control:
library IEEE;
use IEEE.STD_LOGIC_1164.ALL;
use IEEE.NUMERIC_STD.ALL;

entity Control is
    Port (
        JALR_2ndCycle : in  std_logic; -- Entrada especial
        Instr        : in  std_logic_vector(31 downto 0); -- instrução completa

        JALR         : out std_logic;
        JAL          : out std_logic;
        BranchEQ     : out std_logic;
        BranchNEQ    : out std_logic;
        EXSignals    : out std_logic_vector(4 downto 0);	-- ALUOp(2), ALUSrcB, ALUSrcA(2)
        MEMSignals   : out std_logic_vector(1 downto 0);	-- MemWrite, MemRead
        WBSignals    : out std_logic_vector(1 downto 0);	-- RegWrite, MemToReg
        ImmSrc       : out std_logic                     	-- 0 = IMM_GEN, 1 = 4
    );
end Control;

architecture Behavioral of Control is
    signal opcode : std_logic_vector(6 downto 0);
begin
    opcode <= Instr(6 downto 0);  -- extrai opcode da instrução

    process(Instr,JALR_2ndCycle)
        -- sinais temporários
        variable ALUOp    : std_logic_vector(1 downto 0);
        variable ALUSrcA  : std_logic_vector(1 downto 0);
        variable ALUSrcB  : std_logic;
        variable MemRead  : std_logic;
        variable MemWrite : std_logic;
        variable RegWrite : std_logic;
        variable MemToReg : std_logic;
        variable imm1     : std_logic;
        variable isJAL    : std_logic;
        variable isBEQ    : std_logic;
        variable isBNE    : std_logic;
        variable isJALR   : std_logic;
    begin
        -- valores padrão
        ALUOp     := "00";
        ALUSrcA   := "00";
        ALUSrcB   := '0';
        MemRead   := '0';
        MemWrite  := '0';
        RegWrite  := '0';
        MemToReg  := '0';
        imm1      := '0';
        isJAL     := '0';
        isBEQ     := '0';
        isBNE     := '0';
        isJALR    := '0';

        if JALR_2ndCycle = '1' then
            imm1        := '1';           -- força imediato 1
            ALUOp       := "11";          -- ALUOp=00, SrcB=1, SrcA=11 (PC+4)
            ALUSrcA     := "01";
            ALUSrcB     := '1';
            MemWrite    := '0';           -- sem memória
            MemRead     := '0';
            RegWrite    := '1';           -- escreve registrador, via ALU
            MemToReg    := '0';
            isJAL       := '0';
            isBEQ       := '0';
            isBNE       := '0';
				    isJALR      := '0';           -- garante que pipeline não fica presa em JALR
				 else
            case opcode is
                when "0110011" => -- R-type: add, sub, and, or, xor, sll, srl
                    RegWrite  := '1';
                    ALUOp     := "01";
                    ALUSrcB   := '0';
                    ALUSrcA   := "00";

                when "0010011" => -- I-type: addi, andi, ori, xori, slli, srli
                    RegWrite  := '1';
                    ALUOp     := "10";
                    ALUSrcB   := '1';
                    ALUSrcA   := "00";

                when "0000011" => -- lw
                    RegWrite  := '1';
                    MemRead   := '1';
                    MemToReg  := '1';
                    ALUOp     := "11";
                    ALUSrcB   := '1';
                    ALUSrcA   := "00";

                when "0100011" => -- sw
                    MemWrite  := '1';
                    ALUOp     := "11";
                    ALUSrcB   := '1';
                    ALUSrcA   := "00";

                when "1100011" => -- beq, bne
                    ALUOp     := "00"; -- don't care
                    ALUSrcB   := '0';  -- don't care
                    ALUSrcA   := "00"; -- don't care
                    case Instr(14 downto 12) is -- funct3
                        when "000" => isBEQ := '1';  -- beq
                        when "001" => isBNE := '1';  -- bne
                        when others => null;
                    end case;

                when "1101111" => -- jal
                    RegWrite  := '1';
                    ALUOp     := "11";
                    ALUSrcB   := '1';
                    ALUSrcA   := "01"; -- PC + Imm
                    imm1      := '1';
                    isJAL     := '1';

                when "1100111" => -- jalr
                    RegWrite  := '0';
                    ALUOp     := "11";
                    ALUSrcB   := '1';
                    ALUSrcA   := "00"; -- rs1 + Imm
                    isJALR    := '1';

                when "0010111" => -- auipc
                    RegWrite  := '1';
                    ALUOp     := "11";
                    ALUSrcB   := '1';
                    ALUSrcA   := "01"; -- PC + Imm

                when "0110111" => -- lui
                    RegWrite  := '1';
                    ALUOp     := "11";
                    ALUSrcB   := '1';
                    ALUSrcA   := "10";

                when others =>
                    -- valores padrão
            end case;
        end if;

        -- atribuição final aos sinais de saída
        EXSignals  <= ALUOp & ALUSrcB & ALUSrcA;
        MEMSignals <= MemWrite & MemRead;
        WBSignals  <= RegWrite & MemToReg;
        ImmSrc     <= imm1;
        JAL        <= isJAL;
        BranchEQ   <= isBEQ;
        BranchNEQ  <= isBNE;
        JALR       <= isJALR;
    end process;
end Behavioral;
*/

/* Code of HazardUnit:
library IEEE;
use IEEE.STD_LOGIC_1164.ALL;
use IEEE.NUMERIC_STD.ALL;

entity HazardUnit is
    Port (
        ID_EX_MemRead    : in  std_logic;
        ID_EX_RegisterRd : in  std_logic_vector(4 downto 0);
        IF_ID_RegisterRs1: in  std_logic_vector(4 downto 0);
        IF_ID_RegisterRs2: in  std_logic_vector(4 downto 0);

        StallPipeline    : out std_logic
    );
end HazardUnit;

architecture Behavioral of HazardUnit is
begin
    process(ID_EX_MemRead, ID_EX_RegisterRd, IF_ID_RegisterRs1, IF_ID_RegisterRs2)
    begin
        if (ID_EX_MemRead = '1') and
           ((ID_EX_RegisterRd = IF_ID_RegisterRs1) or
            (ID_EX_RegisterRd = IF_ID_RegisterRs2)) then
            StallPipeline <= '1';
        else
            StallPipeline <= '0';
        end if;
    end process;
end Behavioral;
*/

/* Code of PCPlusImm:
library IEEE;
use IEEE.STD_LOGIC_1164.ALL;
use IEEE.NUMERIC_STD.ALL;

entity PCPlusImm is
    Port (
        PC        : in  STD_LOGIC_VECTOR(31 downto 0);
	IMM	  : in  STD_LOGIC_VECTOR(31 downto 0);
        Next_PC   : out  STD_LOGIC_VECTOR(31 downto 0)
    );
end PCPlusImm;

architecture Behavioral of PCPlusImm is
begin
	Next_PC <= std_logic_vector(unsigned(PC) + unsigned(IMM));
end Behavioral;
*/

/* Code of RegisterFile:
LIBRARY ieee;
USE ieee.std_logic_1164.all;
USE ieee.numeric_std.all;

entity RegisterFile is
port (
    	Da: out std_logic_vector (31 downto 0);
    	Db: out std_logic_vector (31 downto 0);
    	Din: in std_logic_vector (31 downto 0);
    	we: in std_logic;
    	Rw: in std_logic_vector (4 downto 0);
    	C: in std_logic;
    	Ra: in std_logic_vector (4 downto 0);
    	Rb: in std_logic_vector (4 downto 0);
	rst: in std_logic
	);
end RegisterFile;

architecture Behavioral of RegisterFile is
    type memoryType is array(0 to (2**5)-1) of STD_LOGIC_VECTOR((31) downto 0);
    signal memory : memoryType;
begin
  process (C, rst)
  begin
	if rst = '1' then
		for i in 0 to 31 loop
			memory(i) <= (others => '0');
		end loop;
    	elsif falling_edge(C) AND (we='1') AND (to_integer(unsigned(Rw)) /= 0) then
      		memory(to_integer(unsigned(Rw))) <= Din;
    	end if;
  end process;
  Da <= memory(to_integer(unsigned(Ra)));
  Db <= memory(to_integer(unsigned(Rb)));
end Behavioral;
*/

/* Code of ImmGen:
library IEEE;
use IEEE.STD_LOGIC_1164.ALL;
use IEEE.NUMERIC_STD.ALL;

entity ImmGen is
    Port (
        Instruction	: in  STD_LOGIC_VECTOR(31 downto 0);
        Immediate   	: out  STD_LOGIC_VECTOR(31 downto 0)
    );
end ImmGen;

architecture Behavioral of ImmGen is

signal opcode : STD_LOGIC_VECTOR(6 downto 0);

begin

opcode <= Instruction(6 downto 0);

process(opcode)
begin
    case opcode is

        when "0110011" =>
		-- R type
		Immediate <= (others => '0');

        when "0010011" | "1100111" | "0000011" =>
		-- I type
		Immediate(31 downto 12) <= (others => Instruction (31)); --bit de sinal
		Immediate (11 downto 0) <= Instruction (31 downto 20);

        when "0010111" | "0110111" => 
            	-- U type
            	Immediate (11 downto 0) <= (others => '0');
		Immediate (31 downto 12) <= Instruction (31 downto 12);

        when "1100011" => 
            	-- SB type
		Immediate (31 downto 12) <= (others => Instruction (31)); --bit de sinal
		Immediate (0) <= '0';
		Immediate (11) <= Instruction (7);
		Immediate (4 downto 1) <= Instruction (11 downto 8);
		Immediate (10 downto 5) <= Instruction (30 downto 25);

        when "1101111" => 
            	-- UJ type
		Immediate (31 downto 20) <= (others => Instruction (31));
		Immediate (0) <= '0';
		Immediate (11) <= Instruction (20);
		Immediate (19 downto 12) <= Instruction (19 downto 12);
		Immediate (10 downto 1) <= Instruction (30 downto 21);
            	
        when "0100011" => 
           	 -- S type
            	Immediate (31 downto 12) <= (others => Instruction (31));
		Immediate (11 downto 5) <= Instruction (31 downto 25);
		Immediate (4 downto 0) <= Instruction (11 downto 7);

        when others =>
            	Immediate <= (others => '0');

    end case;
end process;

end Behavioral;
*/

/* Code of Mux_ControlSignals:
library IEEE;
use IEEE.STD_LOGIC_1164.ALL;

entity Mux_ControlSignals is
    Port (
        stall		: in  std_logic;
        EXSignals_in	: in  STD_LOGIC_VECTOR(4 downto 0);
        MEMSignals_in	: in  STD_LOGIC_VECTOR(1 downto 0);
        WBSignals_in	: in  STD_LOGIC_VECTOR(1 downto 0);
        EXSignals_out	: out STD_LOGIC_VECTOR(4 downto 0);
        MEMSignals_out	: out STD_LOGIC_VECTOR(1 downto 0);
        WBSignals_out	: out STD_LOGIC_VECTOR(1 downto 0)
    );
end Mux_ControlSignals;

architecture Behavorial of Mux_ControlSignals is
begin
    process(EXSignals_in, MEMSignals_in, WBSignals_in, stall)
    begin
        case stall is
            when '0' => 
		EXSignals_out <= EXSignals_in;
		MEMSignals_out <= MEMSignals_in;
		WBSignals_out <= WBSignals_in;
            when others =>
		EXSignals_out <= (others => '0');
		MEMSignals_out <= (others => '0');
		WBSignals_out <= (others => '0');
        end case;
    end process;

end Behavorial;
*/

/* Code of CheckEqual:
library IEEE;
use IEEE.STD_LOGIC_1164.ALL;
use IEEE.NUMERIC_STD.ALL;

entity CheckEqual is
    Port (
        Rs1        : in  STD_LOGIC_VECTOR(31 downto 0);
	Rs2	  : in  STD_LOGIC_VECTOR(31 downto 0);
        IsEqual   : out  STD_LOGIC
    );
end CheckEqual;

architecture Behavioral of CheckEqual is
begin
	IsEqual <= '1' when Rs1 = Rs2 else '0';
end Behavioral;
*/

/* Code of Mux_ImmSrc:
library IEEE;
use IEEE.STD_LOGIC_1164.ALL;
use IEEE.NUMERIC_STD.ALL;

entity Mux_ImmSrc is
    Port (
	SEL	: in  std_logic; -- Linha de seleção
        imm_in	: in  std_logic_vector(31 downto 0); -- Entrada de dados 0
        imm_out	: out std_logic_vector(31 downto 0)  -- Saída de dados
    );
end Mux_ImmSrc;

architecture Behavorial of Mux_ImmSrc is
begin
    process(imm_in, SEL)
    begin
        case SEL is
            when '0'   => imm_out <= imm_in;
            when others =>
		imm_out(0) <= '1';
		imm_out(31 downto 1) <= (others => '0');
        end case;
    end process;

end Behavorial;
*/

/* Code of ID_EX:
library IEEE;
use IEEE.STD_LOGIC_1164.ALL;

entity ID_EX is
    Port ( 
	rst     	: in  STD_LOGIC; 
        clk		: in  STD_LOGIC;

        EXSignals_in	: in  STD_LOGIC_VECTOR(4 downto 0);
        MEMSignals_in	: in  STD_LOGIC_VECTOR(1 downto 0);
        WBSignals_in	: in  STD_LOGIC_VECTOR(1 downto 0);

	PC_in		: in STD_LOGIC_VECTOR(31 downto 0);
        rs1_data_in	: in  STD_LOGIC_VECTOR(31 downto 0);
        rs2_data_in	: in  STD_LOGIC_VECTOR(31 downto 0);
        rd_in		: in  STD_LOGIC_VECTOR(4 downto 0);
        rs1_in		: in  STD_LOGIC_VECTOR(4 downto 0);
        rs2_in		: in  STD_LOGIC_VECTOR(4 downto 0);
	func3_in	: in STD_LOGIC_VECTOR(2 downto 0);
	func7_in	: in STD_LOGIC_VECTOR(6 downto 0);
        immediate_in	: in  STD_LOGIC_VECTOR(31 downto 0);

        rs1_data_out	: out STD_LOGIC_VECTOR(31 downto 0);
        rs2_data_out	: out STD_LOGIC_VECTOR(31 downto 0);
	PC_out		: out STD_LOGIC_VECTOR(31 downto 0);
	immediate_out	: out STD_LOGIC_VECTOR(31 downto 0);
	ALUSrcA		: out STD_LOGIC_VECTOR(1 downto 0);
	ALUSrcB		: out STD_LOGIC;
	func3_out	: out STD_LOGIC_VECTOR(2 downto 0);
	func7_out	: out STD_LOGIC_VECTOR(6 downto 0);
	ALUOp		: out STD_LOGIC_VECTOR(1 downto 0);
	rs1_out		: out STD_LOGIC_VECTOR(4 downto 0);
	rs2_out		: out STD_LOGIC_VECTOR(4 downto 0);
	MemRead		: out STD_LOGIC;
	rd_out		: out STD_LOGIC_VECTOR(4 downto 0);
	MEMSignals_out	: out STD_LOGIC_VECTOR(1 downto 0);
	WBSignals_out	: out STD_LOGIC_VECTOR(1 downto 0)
    );
end ID_EX;

architecture Behavioral of ID_EX is

signal s_dado : STD_LOGIC_VECTOR(31 downto 0);

begin

process(clk,rst)
begin
	if rst = '1' then
		rs1_out <= (others => '0');
		rs2_out <= (others => '0');
		rd_out <= (others => '0');
		MemRead <= '0';
		rs1_data_out <= (others => '0');
		rs2_data_out <= (others => '0');
		func3_out <= (others => '0');
		func7_out <= (others => '0');
		immediate_out <= (others => '0');
		ALUSrcA <= (others => '0');
		ALUSrcB <= '0';
		ALUOp <= (others => '0');
		MEMSignals_out <= (others => '0');
		WBSignals_out <= (others => '0');
        elsif rising_edge(clk) then
		rs1_out <= rs1_in;
		rs2_out <= rs2_in;
		rd_out <= rd_in;
		MemRead <= MEMSignals_in(0);
		rs1_data_out <= rs1_data_in;
		rs2_data_out <= rs2_data_in;
		func3_out <= func3_in;
		func7_out <= func7_in;
		immediate_out <= immediate_in;
		ALUSrcA <= EXSignals_in(1 downto 0);
		ALUSrcB <= EXSignals_in(2);
		ALUOp <= EXSignals_in(4 downto 3);
		MEMSignals_out <= MEMSignals_in;
		WBSignals_out <= WBSignals_in;
	end if;
end process;

end Behavioral;
*/

/* Code of FowardingA:
library IEEE;
use IEEE.STD_LOGIC_1164.ALL;

entity FowardingA is
    Port (
        ID_EX	: in  std_logic_vector(31 downto 0); -- Entrada de dados 0
        EX_MEM	: in  std_logic_vector(31 downto 0); -- Entrada de dados 1
        MEM_WB	: in  std_logic_vector(31 downto 0); -- Entrada de dados 2
        SEL		: in  std_logic_vector(1 downto 0); -- Linha de seleção de 2 bits
        A		: out std_logic_vector(31 downto 0)  -- Saída de dados
    );
end FowardingA;

architecture Behavorial of FowardingA is
begin
    process(ID_EX, EX_MEM, MEM_WB, SEL)
    begin
        case SEL is
            when "00"   => A <= ID_EX;
            when "01"   => A <= EX_MEM;
            when "10"   => A <= MEM_WB;
            when others => A <= (others => '0'); -- casos invalidos
        end case;
    end process;

end Behavorial;
*/

/* Code of FowardingB:
library IEEE;
use IEEE.STD_LOGIC_1164.ALL;

entity FowardingB is
    Port (
        ID_EX	: in  std_logic_vector(31 downto 0); -- Entrada de dados 0
        EX_MEM	: in  std_logic_vector(31 downto 0); -- Entrada de dados 1
        MEM_WB	: in  std_logic_vector(31 downto 0); -- Entrada de dados 2
        SEL		: in  std_logic_vector(1 downto 0); -- Linha de seleção de 2 bits
        B		: out std_logic_vector(31 downto 0)  -- Saída de dados
    );
end FowardingB;

architecture Behavorial of FowardingB is
begin
    process(ID_EX, EX_MEM, MEM_WB, SEL)
    begin
        case SEL is
            when "00"   => B <= ID_EX;
            when "01"   => B <= EX_MEM;
            when "10"   => B <= MEM_WB;
            when others => B <= (others => '0'); -- casos invalidos
        end case;
    end process;

end Behavorial;
*/

/* Code of ALUControl:
library IEEE;
use IEEE.STD_LOGIC_1164.ALL;
use IEEE.NUMERIC_STD.ALL;

entity ALUControl is
    Port (
        ALUOp	: in  std_logic_vector(1 downto 0);
        Funct3	: in  std_logic_vector(2 downto 0);
        Funct7	: in  std_logic_vector(6 downto 0);  -- Bit 30 da instrucao
        ALUCtl	: out std_logic_vector(3 downto 0)
    );
end ALUControl;

architecture Behavioral of ALUControl is
signal Funct7bit5 : std_logic;
begin
Funct7bit5 <= Funct7(5);
    process(ALUOp, Funct3, Funct7bit5)
    begin
        case ALUOp is
	    -- 00: Para instrucoes do tipo branch (BEQ, BNE), usam SUB para comparacao
            when "00" =>
                ALUCtl <= "0110";  -- SUB

            -- 01: Para instrucoes do tipo R-Type (ADD, AND, OR, SLL, SRL, SUB, XOR)
            when "01" =>
		case Funct3 is
                    when "000" =>  -- ADD ou SUB
                        if Funct7bit5 = '0' then
                            ALUCtl <= "0010"; -- ADD
                        else
                            ALUCtl <= "0110"; -- SUB
                        end if;
                    when "111" => ALUCtl <= "0000"; -- AND
                    when "110" => ALUCtl <= "0001"; -- OR
                    when "001" => ALUCtl <= "1000"; -- SLL 
                    when "101" => ALUCtl <= "1001"; -- SRL 
                    when "100" => ALUCtl <= "1100"; -- XOR 
                    when others => ALUCtl <= "1111"; -- invalido
                end case;

            -- 10: Para instrucoes do tipo I-Type (ADDI, ANDI, ORI, SLLI, SRLI, XORI)
            when "10" =>
		case Funct3 is
                    when "000" => ALUCtl <= "0010"; -- ADDI  
                    when "111" => ALUCtl <= "0000"; -- ANDI
                    when "110" => ALUCtl <= "0001"; -- ORI
                    when "001" => ALUCtl <= "1000"; -- SLLI 
                    when "101" => ALUCtl <= "1001"; -- SRLI 
                    when "100" => ALUCtl <= "1100"; -- XORI 
                    when others => ALUCtl <= "1111"; -- invalido
                end case;

            -- 11: Para instrucoes que usam a ALU para soma 
            when "11" =>
                ALUCtl <= "0010"; 

            -- Default
            when others =>
                ALUCtl <= "1111"; -- invalido
        end case;
    end process;
end Behavioral;
*/

/* Code of ForwardingUnit:
library IEEE;
use IEEE.STD_LOGIC_1164.ALL;
use IEEE.NUMERIC_STD.ALL;

entity ForwardingUnit is
    Port (
        ID_EX_RegisterRs1  : in  std_logic_vector(4 downto 0);
        ID_EX_RegisterRs2  : in  std_logic_vector(4 downto 0);

        EX_MEM_RegisterRd  : in  std_logic_vector(4 downto 0);
        EX_MEM_RegWrite    : in  std_logic;

        MEM_WB_RegisterRd  : in  std_logic_vector(4 downto 0);
        MEM_WB_RegWrite    : in  std_logic;

        ForwardA           : out std_logic_vector(1 downto 0);
        ForwardB           : out std_logic_vector(1 downto 0)
    );
end ForwardingUnit;

architecture Behavioral of ForwardingUnit is
begin
    process(ID_EX_RegisterRs1, ID_EX_RegisterRs2, EX_MEM_RegisterRd, EX_MEM_RegWrite,
            MEM_WB_RegisterRd, MEM_WB_RegWrite)
    begin
        -- forwardA, verifica se o rd escreve no registrador, se ele eh o x0 e se ele
				-- eh igual ao registrador source1 que ira ocorrer a execucao
				-- caso essas 3 condicoes sejam cumpridas eh enviado para o MUX de forwardA o sinal 10
				-- esse eh o EX HAZARD:
        if (EX_MEM_RegWrite = '1') and (EX_MEM_RegisterRd /= "00000") and
           (EX_MEM_RegisterRd = ID_EX_RegisterRs1) then
            ForwardA <= "10";
            
        -- esse eh o MEM HAZARD, tem que verificar se eh o foward mais recente, nao pode encaminhar
        -- do MEM se acabou de sair um novo valor do estagio EX.
        elsif (MEM_WB_RegWrite = '1') and (MEM_WB_RegisterRd /= "00000") and
              not (EX_MEM_RegWrite = '1' and EX_MEM_RegisterRd /= "00000" and
                   EX_MEM_RegisterRd = ID_EX_RegisterRs1) and
              (MEM_WB_RegisterRd = ID_EX_RegisterRs1) then
            ForwardA <= "01";
        else
            ForwardA <= "00";
        end if;

        -- mesma coisa que antes mas para o forwardB
        if (EX_MEM_RegWrite = '1') and (EX_MEM_RegisterRd /= "00000") and
           (EX_MEM_RegisterRd = ID_EX_RegisterRs2) then
            ForwardB <= "10";
            
        elsif (MEM_WB_RegWrite = '1') and (MEM_WB_RegisterRd /= "00000") and
              not (EX_MEM_RegWrite = '1' and EX_MEM_RegisterRd /= "00000" and
                   EX_MEM_RegisterRd = ID_EX_RegisterRs2) and
              (MEM_WB_RegisterRd = ID_EX_RegisterRs2) then
            ForwardB <= "01";
        else
            ForwardB <= "00";
        end if;
    end process;
end Behavioral;
*/

/* Code of ALUSrcA:
library IEEE;
use IEEE.STD_LOGIC_1164.ALL;

entity ALUSrcA is
    Port (
        Rs1  	: in  std_logic_vector(31 downto 0); -- Entrada de dados 0
        PC  	: in  std_logic_vector(31 downto 0); -- Entrada de dados 1
        SEL 	: in  std_logic_vector(1 downto 0); -- Linha de seleção de 2 bits
        A   	: out std_logic_vector(31 downto 0)  -- Saída de dados
    );
end ALUSrcA;

architecture Behavorial of ALUSrcA is
begin
    process(Rs1, PC, SEL)
    begin
        case SEL is
            when "00"   => A <= Rs1;
            when "01"   => A <= PC;
            when others => A <= (others => '0'); -- "10" e sinais incorretos
        end case;
    end process;

end Behavorial;
*/

/* Code of ALUSrcB:
library IEEE;
use IEEE.STD_LOGIC_1164.ALL;

entity ALUSrcB is
    Port (
        Rs2  	: in  std_logic_vector(31 downto 0); -- Entrada de dados 0
        imm  	: in  std_logic_vector(31 downto 0); -- Entrada de dados 1
        SEL 	: in  std_logic; -- Linha de seleção
        B   	: out std_logic_vector(31 downto 0)  -- Saída de dados
    );
end ALUSrcB;

architecture Behavorial of ALUSrcB is
begin
    process(Rs2, imm, SEL)
    begin
        case SEL is
            when '0'   => B <= Rs2;
            when others => B <= imm; -- '1'
        end case;
    end process;

end Behavorial;
*/

/* Code of ALU:
library IEEE;
use IEEE.STD_LOGIC_1164.ALL;
use IEEE.NUMERIC_STD.ALL;

entity ALU is
    Port (
        ALUctl  : in  std_logic_vector(3 downto 0);
        A       : in  std_logic_vector(31 downto 0);
        B       : in  std_logic_vector(31 downto 0);
        ALUOut  : out std_logic_vector(31 downto 0)
    );
end ALU;

architecture Behavioral of ALU is
    signal result : std_logic_vector(31 downto 0);
begin

    process(ALUctl, A, B)
        variable A_int : signed(31 downto 0);
        variable B_int : signed(31 downto 0);
        variable B_unsigned : unsigned(31 downto 0);
        variable shift_amt  : integer;
    begin
        A_int := signed(A);
        B_int := signed(B);
        B_unsigned := unsigned(B);
        shift_amt := to_integer(B_unsigned);  -- uso direto de B como deslocamento

        case ALUctl is
            when "0000" => -- AND
                result <= A and B;

            when "0001" => -- OR
                result <= A or B;

            when "0010" => -- ADD
                result <= std_logic_vector(A_int + B_int);

            when "0110" => -- SUB
                result <= std_logic_vector(A_int - B_int);

            when "1000" => -- SLL (Shift Left Logical)
                result <= std_logic_vector(shift_left(unsigned(A), shift_amt));

            when "1001" => -- SRL (Shift Right Logical)
                result <= std_logic_vector(shift_right(unsigned(A), shift_amt));

            when "1100" => -- XOR
                result <= A xor B;

            when others =>
                result <= (others => '0');
        end case;
    end process;

    ALUOut <= result;

end Behavioral;
*/

/* Code of EX_MEM:
library IEEE;
use IEEE.STD_LOGIC_1164.ALL;

entity EX_MEM is
    Port ( 
	rst     	: in  STD_LOGIC; 
        clk		: in  STD_LOGIC;

	ALUoutput_in	: in  STD_LOGIC_VECTOR(31 downto 0);
	rs2_data_in	: in  STD_LOGIC_VECTOR(31 downto 0); --for store instruction
        rd_in		: in  STD_LOGIC_VECTOR(4 downto 0);

	MEMSignals_in	: in STD_LOGIC_VECTOR(1 downto 0);
	WBSignals_in	: in STD_LOGIC_VECTOR(1 downto 0);

	ALUoutput_out	: out  STD_LOGIC_VECTOR(31 downto 0);
        rs2_data_out	: out STD_LOGIC_VECTOR(31 downto 0);
	MemRead		: out STD_LOGIC;
	MemWrite	: out STD_LOGIC;
	rd_out		: out STD_LOGIC_VECTOR(4 downto 0);
	WBSignals_out	: out STD_LOGIC_VECTOR(1 downto 0);
	RegWrite_out	: out STD_LOGIC
    );
end EX_MEM;

architecture Behavioral of EX_MEM is

signal s_dado : STD_LOGIC_VECTOR(31 downto 0);

begin

process(clk,rst)
begin
	if rst = '1' then
		rd_out <= (others => '0');
		rs2_data_out <= (others => '0');
		ALUoutput_out <= (others => '0');
		MemRead <= '0';
		MemWrite <= '0';
		WBSignals_out <= (others => '0');
		RegWrite_out <= '0';
        elsif rising_edge(clk) then
		rd_out <= rd_in;
		rs2_data_out <= rs2_data_in;
		ALUoutput_out <= ALUoutput_in;
		MemRead <= MEMSignals_in(0);
		MemWrite <= MEMSignals_in(1);
		WBSignals_out <= WBSignals_in;
		RegWrite_out <= WBSignals_in(1);
	end if;
end process;

end Behavioral;
*/

/* Code of RAM:
LIBRARY ieee;
USE ieee.std_logic_1164.all;
USE ieee.numeric_std.all;

entity RAM is
  port (
	clk: in std_logic;
	Dout: out std_logic_vector (31 downto 0);
	Addr: in std_logic_vector (31 downto 0);
	Din: in std_logic_vector (31 downto 0);
	Read: in std_logic;
	Write: in std_logic
	);
end RAM;

architecture Behavioral of RAM is
	type memoryType is array(0 to (2**16)-1) of STD_LOGIC_VECTOR(31 downto 0);
	signal memory : memoryType;
	signal A: std_logic_vector (15 downto 0);
begin

A <= Addr(15 downto 0);

process (clk)
begin
	if falling_edge(clk) then
		if Write='1' then
			memory(to_integer(unsigned(A))) <= Din;
		end if;
		if Read='1' then
			Dout <= memory(to_integer(unsigned(A)));
		else
			Dout <= (others => '0');
		end if;
	end if;
end process;

end Behavioral;
*/

/* Code of MEM_WB:
library IEEE;
use IEEE.STD_LOGIC_1164.ALL;

entity MEM_WB is
    Port ( 
	rst     	: in  STD_LOGIC; 
        clk		: in  STD_LOGIC;

        DataFromMem_in	: in  STD_LOGIC_VECTOR(31 downto 0);
	ALUoutput_in	: in  STD_LOGIC_VECTOR(31 downto 0);
        rd_in		: in  STD_LOGIC_VECTOR(4 downto 0);

	WBSignals_in	: in STD_LOGIC_VECTOR(1 downto 0);

	rd_out		: out STD_LOGIC_VECTOR(4 downto 0);
        DataFromMem_out	: out STD_LOGIC_VECTOR(31 downto 0);
	ALUoutput_out	: out  STD_LOGIC_VECTOR(31 downto 0);

	MemToReg 	: out STD_LOGIC;
	RegWrite 	: out STD_LOGIC
    );
end MEM_WB;

architecture Behavioral of MEM_WB is

signal s_dado : STD_LOGIC_VECTOR(31 downto 0);

begin

process(clk,rst)
begin
	if rst = '1' then
		rd_out <= (others => '0');
		DataFromMem_out <= (others => '0');
		ALUoutput_out <= (others => '0');
		MemToReg <= '0';
		RegWrite <= '0';
        elsif rising_edge(clk) then
		rd_out <= rd_in;
		DataFromMem_out <= DataFromMem_in;
		ALUoutput_out <= ALUoutput_in;
		MemToReg <= WBSignals_in(0);
		RegWrite <= WBSignals_in(1);
	end if;
end process;

end Behavioral;
*/

/* Code of MemToReg:
library IEEE;
use IEEE.STD_LOGIC_1164.ALL;

entity MemToReg is
    Port (
        MemOutput	: in  std_logic_vector(31 downto 0); -- Entrada de dados 0
        ALUOutput	: in  std_logic_vector(31 downto 0); -- Entrada de dados 1
        SEL		: in  std_logic; -- Linha de seleção
        DataOut		: out std_logic_vector(31 downto 0)  -- Saída de dados
    );
end MemToReg;

architecture Behavorial of MemToReg is
begin
    process(MemOutput, ALUOutput, SEL)
    begin
        case SEL is
            when '0'   => DataOut <= MemOutput;
            when '1'   => DataOut <= ALUOutput;
            when others => DataOut <= (others => '0'); -- Cobre o caso "11" e outros possíveis (U, X, etc.)
        end case;
    end process;

end Behavorial;
*/
