// Digital circuit CPUcomSIMD.dig as structural Verilog
module CPUcomSIMD (
  input  in_1,
  input  in_2,
  output [31:0] Inst,
  output [31:0] ALUout,
  output [31:0] MEMout,
  output [31:0] DataOut,
  output [31:0] NextPC,
  output [31:0] Inst_2,
  output [4:0] rd
);

  wire and_1_out, and_2_out, or_1_out, or_2_out, or_3_out, u_CheckEqual_isequal, u_Control_brancheq,
       u_Control_branchneq, u_Control_immsrc, u_Control_jal, u_Control_jalr, u_EX_MEM_memread,
       u_EX_MEM_memwrite, u_EX_MEM_regwrite_out, u_HazardUnit_stallpipeline, u_ID_EX_alusrcb,
       u_ID_EX_memread, u_JALR_2ndCycle_FF_jalr_2ndcycle, u_MEM_WB_memtoreg, u_MEM_WB_regwrite;
  wire [1:0] u_Control_memsignals, u_Control_wbsignals, u_EX_MEM_wbsignals_out, u_ForwardingUnit_forwarda,
       u_ForwardingUnit_forwardb, u_ID_EX_alusrca, u_ID_EX_memsignals_out, u_ID_EX_wbsignals_out,
       u_Mux_ControlSignals_memsignals_out, u_Mux_ControlSignals_wbsignals_out;
  wire [2:0] u_ID_EX_aluop, u_ID_EX_func3_out, u_IF_ID_func3;
  wire [3:0] u_ALUControl_aluctl;
  wire [4:0] u_EX_MEM_rd_out, u_ID_EX_rd_out, u_ID_EX_rs1_out, u_ID_EX_rs2_out, u_IF_ID_rd, u_IF_ID_rs1,
       u_IF_ID_rs2;
  wire [5:0] u_Control_exsignals, u_Mux_ControlSignals_exsignals_out;
  wire [6:0] u_ID_EX_func7_out, u_IF_ID_func7;
  wire [15:0] u_PC_pc_out_16b;
  wire [31:0] u_ALUSrcA_a, u_ALUSrcB_b, u_EX_MEM_aluoutput_out, u_EX_MEM_rs2_data_out, u_FowardingA_a,
       u_FowardingB_b, u_ID_EX_immediate_out, u_ID_EX_pc_out, u_ID_EX_rs1_data_out, u_ID_EX_rs2_data_out,
       u_IF_ID_pc_out, u_ImmGen_immediate, u_MEM_WB_aluoutput_out, u_MEM_WB_datafrommem_out,
       u_Mux_ImmSrc_imm_out, u_PC_pc_out, u_PCPlusImm_next_pc, u_PCPlusOne_next_pc, u_RegisterFile_da,
       u_RegisterFile_db;

  or or_1 (or_1_out, and_1_out, and_2_out, u_Control_jal);
  PCSrc #(.applicationType("GHDL")) u_PCSrc (
    .PCplus1(u_PCPlusOne_next_pc), .ID_result(u_PCPlusImm_next_pc), .EX_result(ALUout),
    .S1(u_JALR_2ndCycle_FF_jalr_2ndcycle), .S2(or_1_out), .NextPC(NextPC));
  PCPlusOne #(.applicationType("GHDL")) u_PCPlusOne (.PC(u_PC_pc_out), .Next_PC(u_PCPlusOne_next_pc));
  PC #(.applicationType("GHDL")) u_PC (
    .rst(in_2), .clk(in_1), .PC_in(NextPC), .PC_WRITE(u_HazardUnit_stallpipeline), .PC_out(u_PC_pc_out),
    .PC_out_16b(u_PC_pc_out_16b));
  or or_2 (or_2_out, u_JALR_2ndCycle_FF_jalr_2ndcycle, or_1_out);
  ROM #(.AddrBits(16), .Bits(32)) InstMem (.A(u_PC_pc_out_16b), .sel(1'b1), .D(Inst));
  or or_3 (or_3_out, u_HazardUnit_stallpipeline, u_Control_jalr);
  IF_ID #(.applicationType("GHDL")) u_IF_ID (
    .rst(in_2), .clk(in_1), .IF_ID_WRITE(or_3_out), .IF_ID_flush(or_2_out), .PC_in(u_PC_pc_out),
    .inst_in(Inst), .PC_out(u_IF_ID_pc_out), .inst_out(Inst_2), .rd(u_IF_ID_rd), .rs1(u_IF_ID_rs1),
    .rs2(u_IF_ID_rs2), .func3(u_IF_ID_func3), .func7(u_IF_ID_func7));
  JALR_2ndCycle_FF #(.applicationType("GHDL")) u_JALR_2ndCycle_FF (
    .clk(in_1), .rst(in_2), .JALR_in(u_Control_jalr), .JALR_2ndCycle(u_JALR_2ndCycle_FF_jalr_2ndcycle));
  Control #(.applicationType("GHDL")) u_Control (
    .JALR_2ndCycle(u_JALR_2ndCycle_FF_jalr_2ndcycle), .Instr(Inst_2), .JALR(u_Control_jalr),
    .JAL(u_Control_jal), .BranchEQ(u_Control_brancheq), .BranchNEQ(u_Control_branchneq),
    .EXSignals(u_Control_exsignals), .MEMSignals(u_Control_memsignals), .WBSignals(u_Control_wbsignals),
    .ImmSrc(u_Control_immsrc));
  HazardUnit #(.applicationType("GHDL")) u_HazardUnit (
    .ID_EX_MemRead(u_ID_EX_memread), .ID_EX_RegisterRd(u_ID_EX_rd_out), .IF_ID_RegisterRs1(u_IF_ID_rs1),
    .IF_ID_RegisterRs2(u_IF_ID_rs2), .StallPipeline(u_HazardUnit_stallpipeline));
  PCPlusImm #(.applicationType("GHDL")) u_PCPlusImm (
    .PC(u_IF_ID_pc_out), .IMM(u_ImmGen_immediate), .Next_PC(u_PCPlusImm_next_pc));
  RegisterFile #(.applicationType("GHDL")) u_RegisterFile (
    .Din(DataOut), .we(u_MEM_WB_regwrite), .Rw(rd), .C(in_1), .Ra(u_IF_ID_rs1), .Rb(u_IF_ID_rs2), .rst(in_2),
    .Da(u_RegisterFile_da), .Db(u_RegisterFile_db));
  ImmGen #(.applicationType("GHDL")) u_ImmGen (.Instruction(Inst_2), .Immediate(u_ImmGen_immediate));
  Mux_ControlSignals #(.applicationType("GHDL")) u_Mux_ControlSignals (
    .stall(u_HazardUnit_stallpipeline), .EXSignals_in(u_Control_exsignals),
    .MEMSignals_in(u_Control_memsignals), .WBSignals_in(u_Control_wbsignals),
    .EXSignals_out(u_Mux_ControlSignals_exsignals_out), .MEMSignals_out(u_Mux_ControlSignals_memsignals_out),
    .WBSignals_out(u_Mux_ControlSignals_wbsignals_out));
  CheckEqual #(.applicationType("GHDL")) u_CheckEqual (
    .Rs1(u_RegisterFile_da), .Rs2(u_RegisterFile_db), .IsEqual(u_CheckEqual_isequal));
  and and_1 (and_1_out, u_Control_brancheq, u_CheckEqual_isequal);
  Mux_ImmSrc #(.applicationType("GHDL")) u_Mux_ImmSrc (
    .SEL(u_Control_immsrc), .imm_in(u_ImmGen_immediate), .imm_out(u_Mux_ImmSrc_imm_out));
  and and_2 (and_2_out, ~u_CheckEqual_isequal, u_Control_branchneq);  // And
  ID_EX #(.applicationType("GHDL")) u_ID_EX (
    .rst(in_2), .clk(in_1), .EXSignals_in(u_Mux_ControlSignals_exsignals_out),
    .MEMSignals_in(u_Mux_ControlSignals_memsignals_out), .WBSignals_in(u_Mux_ControlSignals_wbsignals_out),
    .PC_in(u_IF_ID_pc_out), .rs1_data_in(u_RegisterFile_da), .rs2_data_in(u_RegisterFile_db),
    .rd_in(u_IF_ID_rd), .rs1_in(u_IF_ID_rs1), .rs2_in(u_IF_ID_rs2), .func3_in(u_IF_ID_func3),
    .func7_in(u_IF_ID_func7), .immediate_in(u_Mux_ImmSrc_imm_out), .rs1_data_out(u_ID_EX_rs1_data_out),
    .rs2_data_out(u_ID_EX_rs2_data_out), .PC_out(u_ID_EX_pc_out), .immediate_out(u_ID_EX_immediate_out),
    .ALUSrcA(u_ID_EX_alusrca), .ALUSrcB(u_ID_EX_alusrcb), .func3_out(u_ID_EX_func3_out),
    .func7_out(u_ID_EX_func7_out), .ALUOp(u_ID_EX_aluop), .rs1_out(u_ID_EX_rs1_out),
    .rs2_out(u_ID_EX_rs2_out), .MemRead(u_ID_EX_memread), .rd_out(u_ID_EX_rd_out),
    .MEMSignals_out(u_ID_EX_memsignals_out), .WBSignals_out(u_ID_EX_wbsignals_out));
  FowardingA #(.applicationType("GHDL")) u_FowardingA (
    .ID_EX(u_ID_EX_rs1_data_out), .EX_MEM(u_EX_MEM_aluoutput_out), .MEM_WB(DataOut),
    .SEL(u_ForwardingUnit_forwarda), .A(u_FowardingA_a));
  FowardingB #(.applicationType("GHDL")) u_FowardingB (
    .ID_EX(u_ID_EX_rs2_data_out), .EX_MEM(u_EX_MEM_aluoutput_out), .MEM_WB(DataOut),
    .SEL(u_ForwardingUnit_forwardb), .B(u_FowardingB_b));
  ALUControl #(.applicationType("GHDL")) u_ALUControl (
    .ALUOp(u_ID_EX_aluop), .Funct3(u_ID_EX_func3_out), .Funct7(u_ID_EX_func7_out),
    .ALUCtl(u_ALUControl_aluctl));
  ForwardingUnit #(.applicationType("GHDL")) u_ForwardingUnit (
    .ID_EX_RegisterRs1(u_ID_EX_rs1_out), .ID_EX_RegisterRs2(u_ID_EX_rs2_out),
    .EX_MEM_RegisterRd(u_EX_MEM_rd_out), .EX_MEM_RegWrite(u_EX_MEM_regwrite_out), .MEM_WB_RegisterRd(rd),
    .MEM_WB_RegWrite(u_MEM_WB_regwrite), .ForwardA(u_ForwardingUnit_forwarda),
    .ForwardB(u_ForwardingUnit_forwardb));
  ALUSrcA #(.applicationType("GHDL")) u_ALUSrcA (
    .Rs1(u_FowardingA_a), .PC(u_ID_EX_pc_out), .SEL(u_ID_EX_alusrca), .A(u_ALUSrcA_a));
  ALUSrcB #(.applicationType("GHDL")) u_ALUSrcB (
    .Rs2(u_FowardingB_b), .imm(u_ID_EX_immediate_out), .SEL(u_ID_EX_alusrcb), .B(u_ALUSrcB_b));
  ALU #(.applicationType("GHDL")) u_ALU (
    .Funct3(u_ID_EX_func3_out), .ALUctl(u_ALUControl_aluctl), .A(u_ALUSrcA_a), .B(u_ALUSrcB_b),
    .ALUOut(ALUout));
  EX_MEM #(.applicationType("GHDL")) u_EX_MEM (
    .rst(in_2), .clk(in_1), .ALUoutput_in(ALUout), .rs2_data_in(u_FowardingB_b), .rd_in(u_ID_EX_rd_out),
    .MEMSignals_in(u_ID_EX_memsignals_out), .WBSignals_in(u_ID_EX_wbsignals_out),
    .ALUoutput_out(u_EX_MEM_aluoutput_out), .rs2_data_out(u_EX_MEM_rs2_data_out), .MemRead(u_EX_MEM_memread),
    .MemWrite(u_EX_MEM_memwrite), .rd_out(u_EX_MEM_rd_out), .WBSignals_out(u_EX_MEM_wbsignals_out),
    .RegWrite_out(u_EX_MEM_regwrite_out));
  RAM #(.applicationType("GHDL")) u_RAM (
    .clk(in_1), .Addr(u_EX_MEM_aluoutput_out), .Din(u_EX_MEM_rs2_data_out), .Read(u_EX_MEM_memread),
    .Write(u_EX_MEM_memwrite), .Dout(MEMout));
  MEM_WB #(.applicationType("GHDL")) u_MEM_WB (
    .rst(in_2), .clk(in_1), .DataFromMem_in(MEMout), .ALUoutput_in(u_EX_MEM_aluoutput_out),
    .rd_in(u_EX_MEM_rd_out), .WBSignals_in(u_EX_MEM_wbsignals_out), .rd_out(rd),
    .DataFromMem_out(u_MEM_WB_datafrommem_out), .ALUoutput_out(u_MEM_WB_aluoutput_out),
    .MemToReg(u_MEM_WB_memtoreg), .RegWrite(u_MEM_WB_regwrite));
  MemToReg #(.applicationType("GHDL")) u_MemToReg (
    .MemOutput(u_MEM_WB_datafrommem_out), .ALUOutput(u_MEM_WB_aluoutput_out), .SEL(u_MEM_WB_memtoreg),
    .DataOut(DataOut));

  // Other names for the same wires on the sheet: CLK = in_1; RST = in_2

  // Notes on the sheet:
  //   contents of InstMem (hex, n*v repeats v):
  //   0,800093,40e113,417193,a14213,209293,100563,20d313,1020a3,3103b3
  //   ,417433,4164b3,414533,401105b3,619633,819563,62d6b3,102703,818363
  //   ,5*100993,311363,5*100993,1797,2837,6008ef,5*100993,c28967,5*100993
  //   ,ffc08a13,a2a83,a8b33,0,100bf8,1b8c79
endmodule

/* Code of PCSrc:
library IEEE;
use IEEE.STD_LOGIC_1164.ALL;

entity PCSrc is
    Port (
        PCplus1  : in  std_logic_vector(31 downto 0);
        ID_result: in  std_logic_vector(31 downto 0);
        EX_result: in  std_logic_vector(31 downto 0);
        S1       : in  std_logic;
        S2       : in  std_logic;
        NextPC   : out std_logic_vector(31 downto 0)
    );
end PCSrc;

architecture Behavorial of PCSrc is
    signal SEL : std_logic_vector(1 downto 0);
begin

    SEL <= S1 & S2;

    with SEL select
        NextPC <= PCplus1   when "00",
                  ID_result when "01",
                  EX_result when "10",
                  (others => '0') when others;

end Behavorial;
*/

/* Code of PCPlusOne:
library IEEE;
use IEEE.STD_LOGIC_1164.ALL;
use IEEE.NUMERIC_STD.ALL;

entity PCPlusOne is
    Port (
        PC        : in  STD_LOGIC_VECTOR(31 downto 0);
        Next_PC   : out  STD_LOGIC_VECTOR(31 downto 0)
    );
end PCPlusOne;

architecture Behavioral of PCPlusOne is
begin
	Next_PC <= std_logic_vector(unsigned(PC) + 1);
end Behavioral;
*/

/* Code of PC:
library IEEE;
use IEEE.STD_LOGIC_1164.ALL;

entity PC is
    Port ( 
	rst     	: in  STD_LOGIC; 
        clk		: in  STD_LOGIC;

        PC_in		: in  STD_LOGIC_VECTOR(31 downto 0);
	PC_WRITE	: in STD_LOGIC;
	PC_out		: out STD_LOGIC_VECTOR(31 downto 0);
	PC_out_16b	: out STD_LOGIC_VECTOR(15 downto 0)
    );
end PC;

architecture Behavioral of PC is

signal s_dado : STD_LOGIC_VECTOR(31 downto 0);

begin

process(clk,rst)
begin
	if rst = '1' then
		PC_out <= (others => '0');
        elsif rising_edge(clk) and PC_WRITE='0' then
		PC_out <= PC_in;
	end if;
end process;

PC_out_16b <= PC_out(15 downto 0);

end Behavioral;
*/

/* Code of IF_ID:
library IEEE;
use IEEE.STD_LOGIC_1164.ALL;

entity IF_ID is
    Port ( 
	rst     	: in  STD_LOGIC; 
        clk		: in  STD_LOGIC;

	IF_ID_WRITE	: in STD_LOGIC;
	IF_ID_flush	: in STD_LOGIC;
        PC_in		: in  STD_LOGIC_VECTOR(31 downto 0);
        inst_in		: in  STD_LOGIC_VECTOR(31 downto 0);

	PC_out		: out STD_LOGIC_VECTOR(31 downto 0);
	inst_out	: out STD_LOGIC_VECTOR(31 downto 0);
	rd		: out STD_LOGIC_VECTOR(4 downto 0);
        rs1		: out STD_LOGIC_VECTOR(4 downto 0);
        rs2		: out STD_LOGIC_VECTOR(4 downto 0);
	func3		: out STD_LOGIC_VECTOR(2 downto 0);
	func7		: out STD_LOGIC_VECTOR(6 downto 0)

    );
end IF_ID;

architecture Behavioral of IF_ID is

signal s_dado : STD_LOGIC_VECTOR(31 downto 0);

begin

process(clk,rst)
begin
	if rst = '1' then
		s_dado <= (others => '0');
        elsif rising_edge(clk) and IF_ID_WRITE='0' then
		if IF_ID_flush='1' then
			PC_out <= (others => '0');
			inst_out <= (others => '0');
		else
			PC_out <= PC_in;
            		inst_out <= inst_in;
		end if;
	end if;
end process;

rs1 <= inst_out(19 downto 15);
rs2 <= inst_out(24 downto 20);
rd <= inst_out(11 downto 7);
func3 <= inst_out(14 downto 12);
func7 <= inst_out(31 downto 25);

end Behavioral;
*/

/* Code of JALR_2ndCycle_FF:
library IEEE;
use IEEE.STD_LOGIC_1164.ALL;

entity JALR_2ndCycle_FF is
    Port (
        clk          : in  std_logic;
        rst          : in  std_logic;
        JALR_in      : in  std_logic;  -- sinal JALR do Control
        JALR_2ndCycle: out std_logic   -- sinal que indica o 2º ciclo
    );
end JALR_2ndCycle_FF;

architecture Behavioral of JALR_2ndCycle_FF is
    signal jalr_reg : std_logic := '0';
begin
    process(clk, rst)
    begin
        if rst = '1' then
            jalr_reg <= '0';
        elsif rising_edge(clk) then
            jalr_reg <= JALR_in;
        end if;
    end process;

    JALR_2ndCycle <= jalr_reg;
end Behavioral;
*/

/* Code of Control:
library IEEE;
use IEEE.STD_LOGIC_1164.ALL;
use IEEE.NUMERIC_STD.ALL;

entity Control is
    Port (
        JALR_2ndCycle : in  std_logic;
        Instr         : in  std_logic_vector(31 downto 0);

        JALR          : out std_logic;
        JAL           : out std_logic;
        BranchEQ      : out std_logic;
        BranchNEQ     : out std_logic;
        EXSignals     : out std_logic_vector(5 downto 0);  -- ALUOp(3), ALUSrcB, ALUSrcA(2)
        MEMSignals    : out std_logic_vector(1 downto 0);  -- MemWrite, MemRead
        WBSignals     : out std_logic_vector(1 downto 0);  -- RegWrite, MemToReg
        ImmSrc        : out std_logic                      -- 0 = IMM_GEN, 1 = 4
    );
end Control;

architecture Behavioral of Control is
    signal opcode  : std_logic_vector(6 downto 0);
    signal funct3  : std_logic_vector(2 downto 0);

    signal ALUOp     : std_logic_vector(2 downto 0);
    signal ALUSrcA   : std_logic_vector(1 downto 0);
    signal ALUSrcB   : std_logic;
    signal MemRead   : std_logic;
    signal MemWrite  : std_logic;
    signal RegWrite  : std_logic;
    signal MemToReg  : std_logic;
    signal imm4      : std_logic;
    signal isJAL     : std_logic;
    signal isBEQ     : std_logic;
    signal isBNE     : std_logic;
    signal isJALR    : std_logic;
begin

    opcode <= Instr(6 downto 0);
    funct3 <= Instr(14 downto 12);

    -- ALUOp
    ALUOp <= "011" when JALR_2ndCycle = '1' else
             "001" when opcode = "0110011" else
             "010" when opcode = "0010011" else
             "011" when opcode = "0000011" or
                              opcode = "0100011" or
                              opcode = "1101111" or
                              opcode = "1100111" or
                              opcode = "0010111" or
                              opcode = "0110111" else
             "100" when opcode = "1110000" or
                              opcode = "1111000" else
             "101" when opcode = "1110001" or
                              opcode = "1111001" else
             "000";

    -- ALUSrcA
    ALUSrcA <= "01" when JALR_2ndCycle = '1' else
               "00" when opcode = "0110011" or
                            opcode = "0010011" or
                            opcode = "0000011" or
                            opcode = "0100011" or
                            opcode = "1100111" or
                            opcode = "1110000" or
                            opcode = "1110001" or
                            opcode = "1111000" or
                            opcode = "1111001" else
               "01" when opcode = "1101111" or
                                opcode = "0010111" else
               "10" when opcode = "0110111" else
               "00";

    -- ALUSrcB
    ALUSrcB <= '1' when JALR_2ndCycle = '1' or
                        opcode = "0010011" or
                        opcode = "0000011" or
                        opcode = "0100011" or
                        opcode = "1101111" or
                        opcode = "1100111" or
                        opcode = "0010111" or
                        opcode = "0110111" or
                        opcode = "1111000" or
                        opcode = "1111001"
               else '0';

    -- MemRead e MemWrite
    MemRead  <= '1' when JALR_2ndCycle = '0' and opcode = "0000011" else '0';
    MemWrite <= '1' when JALR_2ndCycle = '0' and opcode = "0100011" else '0';

    -- RegWrite
    RegWrite <= '1' when JALR_2ndCycle = '1' or
                        opcode = "0110011" or
                        opcode = "0010011" or
                        opcode = "0000011" or
                        opcode = "1101111" or
                        opcode = "0010111" or
                        opcode = "0110111" or
                        opcode = "1110000" or
                        opcode = "1110001" or
                        opcode = "1111000" or
                        opcode = "1111001"
                else '0';

    -- MemToReg
    MemToReg <= '1' when JALR_2ndCycle = '0' and opcode = "0000011" else '0';

    -- ImmSrc (se usa 4)
    ImmSrc <= '1' when JALR_2ndCycle = '1' or opcode = "1101111" else '0';

    -- JAL
    JAL <= '1' when JALR_2ndCycle = '0' and opcode = "1101111" else '0';

    -- JALR
    JALR <= '1' when JALR_2ndCycle = '0' and opcode = "1100111" else '0';

    -- BranchEQ e BranchNEQ
    BranchEQ <= '1' when JALR_2ndCycle = '0' and opcode = "1100011" and funct3 = "000" else '0';
    BranchNEQ <= '1' when JALR_2ndCycle = '0' and opcode = "1100011" and funct3 = "001" else '0';

    -- Saídas finais
    EXSignals  <= ALUOp & ALUSrcB & ALUSrcA;
    MEMSignals <= MemWrite & MemRead;
    WBSignals  <= RegWrite & MemToReg;

end Behavioral;
*/

/* Code of HazardUnit:
library IEEE;
use IEEE.STD_LOGIC_1164.ALL;
use IEEE.NUMERIC_STD.ALL;

entity HazardUnit is
    Port (
        ID_EX_MemRead    : in  std_logic;
        ID_EX_RegisterRd : in  std_logic_vector(4 downto 0);
        IF_ID_RegisterRs1: in  std_logic_vector(4 downto 0);
        IF_ID_RegisterRs2: in  std_logic_vector(4 downto 0);

        StallPipeline    : out std_logic
    );
end HazardUnit;

architecture Behavioral of HazardUnit is
begin
    process(ID_EX_MemRead, ID_EX_RegisterRd, IF_ID_RegisterRs1, IF_ID_RegisterRs2)
    begin
        if (ID_EX_MemRead = '1') and
           ((ID_EX_RegisterRd = IF_ID_RegisterRs1) or
            (ID_EX_RegisterRd = IF_ID_RegisterRs2)) then
            StallPipeline <= '1';
        else
            StallPipeline <= '0';
        end if;
    end process;
end Behavioral;
*/

/* Code of PCPlusImm:
library IEEE;
use IEEE.STD_LOGIC_1164.ALL;
use IEEE.NUMERIC_STD.ALL;

entity PCPlusImm is
    Port (
        PC        : in  STD_LOGIC_VECTOR(31 downto 0);
	IMM	  : in  STD_LOGIC_VECTOR(31 downto 0);
        Next_PC   : out  STD_LOGIC_VECTOR(31 downto 0)
    );
end PCPlusImm;

architecture Behavioral of PCPlusImm is
begin
	Next_PC <= std_logic_vector(unsigned(PC) + unsigned(IMM));
end Behavioral;
*/

/* Code of RegisterFile:
LIBRARY ieee;
USE ieee.std_logic_1164.all;
USE ieee.numeric_std.all;

entity RegisterFile is
port (
    	Da: out std_logic_vector (31 downto 0);
    	Db: out std_logic_vector (31 downto 0);
    	Din: in std_logic_vector (31 downto 0);
    	we: in std_logic;
    	Rw: in std_logic_vector (4 downto 0);
    	C: in std_logic;
    	Ra: in std_logic_vector (4 downto 0);
    	Rb: in std_logic_vector (4 downto 0);
	rst: in std_logic
	);
end RegisterFile;

architecture Behavioral of RegisterFile is
    type memoryType is array(0 to (2**5)-1) of STD_LOGIC_VECTOR((31) downto 0);
    signal memory : memoryType;
begin
  process (C, rst)
  begin
	if rst = '1' then
		for i in 0 to 31 loop
			memory(i) <= (others => '0');
		end loop;
    	elsif falling_edge(C) AND (we='1') AND (to_integer(unsigned(Rw)) /= 0) then
      		memory(to_integer(unsigned(Rw))) <= Din;
    	end if;
  end process;
  Da <= memory(to_integer(unsigned(Ra)));
  Db <= memory(to_integer(unsigned(Rb)));
end Behavioral;
*/

/* Code of ImmGen:
library IEEE;
use IEEE.STD_LOGIC_1164.ALL;
use IEEE.NUMERIC_STD.ALL;

entity ImmGen is
    Port (
        Instruction : in  STD_LOGIC_VECTOR(31 downto 0);
        Immediate   : out STD_LOGIC_VECTOR(31 downto 0)
    );
end ImmGen;

architecture Behavioral of ImmGen is
    signal opcode    : STD_LOGIC_VECTOR(6 downto 0);
    signal vec_size  : STD_LOGIC_VECTOR(1 downto 0); -- bits 13 e 12 (LSBs de funct3)
begin

    opcode    <= Instruction(6 downto 0);
    vec_size  <= Instruction(13 downto 12);

    process(opcode, Instruction)
        variable imm_part : STD_LOGIC_VECTOR(31 downto 0);
    begin
        case opcode is
            -- Instruções tipo R (sem imediato)
            when "0110011" =>
                Immediate <= (others => '0');

            -- Instruções tipo I (addi, lw, jalr, etc.)
            when "0010011" | "1100111" | "0000011" =>
                Immediate(11 downto 0)  <= Instruction(31 downto 20);
                Immediate(31 downto 12) <= (others => Instruction(31)); -- sign-extend

            -- Instruções tipo S (sw)
            when "0100011" =>
                Immediate(4 downto 0)   <= Instruction(11 downto 7);
                Immediate(11 downto 5)  <= Instruction(31 downto 25);
                Immediate(31 downto 12) <= (others => Instruction(31));

            -- Instruções tipo SB (beq, bne)
            when "1100011" =>
                Immediate(0)            <= '0';
                Immediate(4 downto 1)   <= Instruction(11 downto 8);
                Immediate(10 downto 5)  <= Instruction(30 downto 25);
                Immediate(11)           <= Instruction(7);
                Immediate(31 downto 12) <= (others => Instruction(31));

            -- Instruções tipo UJ (jal)
            when "1101111" =>
                Immediate(0)            <= '0';
                Immediate(10 downto 1)  <= Instruction(30 downto 21);
                Immediate(11)           <= Instruction(20);
                Immediate(19 downto 12) <= Instruction(19 downto 12);
                Immediate(31 downto 20) <= (others => Instruction(31));

            -- Instruções tipo U (auipc, lui)
            when "0010111" | "0110111" =>
                Immediate(11 downto 0)  <= (others => '0');
                Immediate(31 downto 12) <= Instruction(31 downto 12);

            -- Instruções vetoriais tipo R/I (opcode específicos)
            when "1110000" | "1110001" | "1111000" | "1111001" =>
                case vec_size is
                    when "00" =>  -- vetor de 4 bits replicado 8x
                        imm_part(3 downto 0) := Instruction(23 downto 20);
                        Immediate <= imm_part(3 downto 0) & imm_part(3 downto 0) &
                                     imm_part(3 downto 0) & imm_part(3 downto 0) &
                                     imm_part(3 downto 0) & imm_part(3 downto 0) &
                                     imm_part(3 downto 0) & imm_part(3 downto 0);

                    when "01" =>  -- vetor de 8 bits replicado 4x
                        imm_part(7 downto 0) := Instruction(27 downto 20);
                        Immediate <= imm_part(7 downto 0) & imm_part(7 downto 0) &
                                     imm_part(7 downto 0) & imm_part(7 downto 0);

                    when "10" =>  -- vetor de 16 bits replicado 2x
                        imm_part(15 downto 12) := (others => Instruction(31)); --replica bit de sinal
                        imm_part(11 downto 0) := Instruction(31 downto 20);
                        Immediate <= imm_part(15 downto 0) & imm_part(15 downto 0);

                    when "11" =>  -- vetor de 32 bits: usar os 12 bits do imediato (I-type) com sign-extend
                        imm_part(31 downto 12) := (others => Instruction(31)); --replica bit de sinal
                        imm_part(11 downto 0) := Instruction(31 downto 20);
                        Immediate <= imm_part;

                    when others =>
                        Immediate <= (others => '0');
                end case;

            -- Instruções desconhecidas
            when others =>
                Immediate <= (others => '0');
        end case;
    end process;

end Behavioral;
*/

/* Code of Mux_ControlSignals:
library IEEE;
use IEEE.STD_LOGIC_1164.ALL;

entity Mux_ControlSignals is
    Port (
        stall		: in  std_logic;
        EXSignals_in	: in  STD_LOGIC_VECTOR(5 downto 0);
        MEMSignals_in	: in  STD_LOGIC_VECTOR(1 downto 0);
        WBSignals_in	: in  STD_LOGIC_VECTOR(1 downto 0);
        EXSignals_out	: out STD_LOGIC_VECTOR(5 downto 0);
        MEMSignals_out	: out STD_LOGIC_VECTOR(1 downto 0);
        WBSignals_out	: out STD_LOGIC_VECTOR(1 downto 0)
    );
end Mux_ControlSignals;

architecture Behavorial of Mux_ControlSignals is
begin
    process(EXSignals_in, MEMSignals_in, WBSignals_in, stall)
    begin
        case stall is
            when '0' => 
		EXSignals_out <= EXSignals_in;
		MEMSignals_out <= MEMSignals_in;
		WBSignals_out <= WBSignals_in;
            when others =>
		EXSignals_out <= (others => '0');
		MEMSignals_out <= (others => '0');
		WBSignals_out <= (others => '0');
        end case;
    end process;

end Behavorial;
*/

/* Code of CheckEqual:
library IEEE;
use IEEE.STD_LOGIC_1164.ALL;
use IEEE.NUMERIC_STD.ALL;

entity CheckEqual is
    Port (
        Rs1        : in  STD_LOGIC_VECTOR(31 downto 0);
	Rs2	  : in  STD_LOGIC_VECTOR(31 downto 0);
        IsEqual   : out  STD_LOGIC
    );
end CheckEqual;

architecture Behavioral of CheckEqual is
begin
	IsEqual <= '1' when Rs1 = Rs2 else '0';
end Behavioral;
*/

/* Code of Mux_ImmSrc:
library IEEE;
use IEEE.STD_LOGIC_1164.ALL;
use IEEE.NUMERIC_STD.ALL;

entity Mux_ImmSrc is
    Port (
	SEL	: in  std_logic; -- Linha de seleção
        imm_in	: in  std_logic_vector(31 downto 0); -- Entrada de dados 0
        imm_out	: out std_logic_vector(31 downto 0)  -- Saída de dados
    );
end Mux_ImmSrc;

architecture Behavorial of Mux_ImmSrc is
begin
    process(imm_in, SEL)
    begin
        case SEL is
            when '0'   => imm_out <= imm_in;
            when others =>
		imm_out(0) <= '1';
		imm_out(31 downto 1) <= (others => '0');
        end case;
    end process;

end Behavorial;
*/

/* Code of ID_EX:
library IEEE;
use IEEE.STD_LOGIC_1164.ALL;

entity ID_EX is
    Port ( 
	rst     	: in  STD_LOGIC; 
        clk		: in  STD_LOGIC;

        EXSignals_in	: in  STD_LOGIC_VECTOR(5 downto 0);
        MEMSignals_in	: in  STD_LOGIC_VECTOR(1 downto 0);
        WBSignals_in	: in  STD_LOGIC_VECTOR(1 downto 0);

	PC_in		: in STD_LOGIC_VECTOR(31 downto 0);
        rs1_data_in	: in  STD_LOGIC_VECTOR(31 downto 0);
        rs2_data_in	: in  STD_LOGIC_VECTOR(31 downto 0);
        rd_in		: in  STD_LOGIC_VECTOR(4 downto 0);
        rs1_in		: in  STD_LOGIC_VECTOR(4 downto 0);
        rs2_in		: in  STD_LOGIC_VECTOR(4 downto 0);
	func3_in	: in STD_LOGIC_VECTOR(2 downto 0);
	func7_in	: in STD_LOGIC_VECTOR(6 downto 0);
        immediate_in	: in  STD_LOGIC_VECTOR(31 downto 0);

        rs1_data_out	: out STD_LOGIC_VECTOR(31 downto 0);
        rs2_data_out	: out STD_LOGIC_VECTOR(31 downto 0);
	PC_out		: out STD_LOGIC_VECTOR(31 downto 0);
	immediate_out	: out STD_LOGIC_VECTOR(31 downto 0);
	ALUSrcA		: out STD_LOGIC_VECTOR(1 downto 0);
	ALUSrcB		: out STD_LOGIC;
	func3_out	: out STD_LOGIC_VECTOR(2 downto 0);
	func7_out	: out STD_LOGIC_VECTOR(6 downto 0);
	ALUOp		: out STD_LOGIC_VECTOR(2 downto 0);
	rs1_out		: out STD_LOGIC_VECTOR(4 downto 0);
	rs2_out		: out STD_LOGIC_VECTOR(4 downto 0);
	MemRead		: out STD_LOGIC;
	rd_out		: out STD_LOGIC_VECTOR(4 downto 0);
	MEMSignals_out	: out STD_LOGIC_VECTOR(1 downto 0);
	WBSignals_out	: out STD_LOGIC_VECTOR(1 downto 0)
    );
end ID_EX;

architecture Behavioral of ID_EX is

signal s_dado : STD_LOGIC_VECTOR(31 downto 0);

begin

process(clk,rst)
begin
	if rst = '1' then
		rs1_out <= (others => '0');
		rs2_out <= (others => '0');
		rd_out <= (others => '0');
		PC_out <= (others => '0');
		MemRead <= '0';
		rs1_data_out <= (others => '0');
		rs2_data_out <= (others => '0');
		func3_out <= (others => '0');
		func7_out <= (others => '0');
		immediate_out <= (others => '0');
		ALUSrcA <= (others => '0');
		ALUSrcB <= '0';
		ALUOp <= (others => '0');
		MEMSignals_out <= (others => '0');
		WBSignals_out <= (others => '0');
        elsif rising_edge(clk) then
		rs1_out <= rs1_in;
		rs2_out <= rs2_in;
		rd_out <= rd_in;
		PC_out <= PC_in;
		MemRead <= MEMSignals_in(0);
		rs1_data_out <= rs1_data_in;
		rs2_data_out <= rs2_data_in;
		func3_out <= func3_in;
		func7_out <= func7_in;
		immediate_out <= immediate_in;
		ALUSrcA <= EXSignals_in(1 downto 0);
		ALUSrcB <= EXSignals_in(2);
		ALUOp <= EXSignals_in(5 downto 3);
		MEMSignals_out <= MEMSignals_in;
		WBSignals_out <= WBSignals_in;
	end if;
end process;

end Behavioral;
*/

/* Code of FowardingA:
library IEEE;
use IEEE.STD_LOGIC_1164.ALL;

entity FowardingA is
    Port (
        ID_EX	: in  std_logic_vector(31 downto 0); -- Entrada de dados 0
        EX_MEM	: in  std_logic_vector(31 downto 0); -- Entrada de dados 1
        MEM_WB	: in  std_logic_vector(31 downto 0); -- Entrada de dados 2
        SEL		: in  std_logic_vector(1 downto 0); -- Linha de seleção de 2 bits
        A		: out std_logic_vector(31 downto 0)  -- Saída de dados
    );
end FowardingA;

architecture Behavorial of FowardingA is
begin
    process(ID_EX, EX_MEM, MEM_WB, SEL)
    begin
        case SEL is
            when "00"   => A <= ID_EX;
            when "10"   => A <= EX_MEM;
            when "01"   => A <= MEM_WB;
            when others => A <= (others => '0'); -- casos invalidos
        end case;
    end process;

end Behavorial;
*/

/* Code of FowardingB:
library IEEE;
use IEEE.STD_LOGIC_1164.ALL;

entity FowardingB is
    Port (
        ID_EX	: in  std_logic_vector(31 downto 0); -- Entrada de dados 0
        EX_MEM	: in  std_logic_vector(31 downto 0); -- Entrada de dados 1
        MEM_WB	: in  std_logic_vector(31 downto 0); -- Entrada de dados 2
        SEL		: in  std_logic_vector(1 downto 0); -- Linha de seleção de 2 bits
        B		: out std_logic_vector(31 downto 0)  -- Saída de dados
    );
end FowardingB;

architecture Behavorial of FowardingB is
begin
    process(ID_EX, EX_MEM, MEM_WB, SEL)
    begin
        case SEL is
            when "00"   => B <= ID_EX;
            when "10"   => B <= EX_MEM;
            when "01"   => B <= MEM_WB;
            when others => B <= (others => '0'); -- casos invalidos
        end case;
    end process;

end Behavorial;
*/

/* Code of ALUControl:
library IEEE;
use IEEE.STD_LOGIC_1164.ALL;
use IEEE.NUMERIC_STD.ALL;

entity ALUControl is
    Port (
        ALUOp      : in  std_logic_vector(2 downto 0);
        Funct3     : in  std_logic_vector(2 downto 0);
        Funct7     : in  std_logic_vector(6 downto 0);
        ALUCtl     : out std_logic_vector(3 downto 0)
    );
end ALUControl;

architecture Behavioral of ALUControl is
signal Funct7bit5 : std_logic;
begin
Funct7bit5 <= Funct7(5);
    process(ALUOp, Funct3, Funct7bit5)
    begin
        case ALUOp is
	    -- 000: Para instrucoes do tipo branch (BEQ, BNE), usam SUB para comparacao
            when "000" =>
                ALUCtl <= "0110";  -- SUB

            -- 001: Para instrucoes do tipo R-Type (ADD, AND, OR, SLL, SRL, SUB, XOR)NAO VETORIAL
            when "001" =>
		case Funct3 is
                    when "000" =>  -- ADD ou SUB
                        if Funct7bit5 = '0' then
                            ALUCtl <= "0010"; -- ADD
                        else
                            ALUCtl <= "0110"; -- SUB
                        end if;
                    when "111" => ALUCtl <= "0000"; -- AND
                    when "110" => ALUCtl <= "0001"; -- OR
                    when "001" => ALUCtl <= "1000"; -- SLL 
                    when "101" => ALUCtl <= "1001"; -- SRL 
                    when "100" => ALUCtl <= "1100"; -- XOR 
                    when others => ALUCtl <= "1111"; -- invalido
                end case;

            -- 010: Para instrucoes do tipo I-Type (ADDI, ANDI, ORI, SLLI, SRLI, XORI)NAO VETORIAIS
            when "010" =>
		case Funct3 is
                    when "000" => ALUCtl <= "0010"; -- ADDI  
                    when "111" => ALUCtl <= "0000"; -- ANDI
                    when "110" => ALUCtl <= "0001"; -- ORI
                    when "001" => ALUCtl <= "1000"; -- SLLI 
                    when "101" => ALUCtl <= "1001"; -- SRLI 
                    when "100" => ALUCtl <= "1100"; -- XORI 
                    when others => ALUCtl <= "1111"; -- invalido
                end case;

            -- 011: Para instrucoes que usam a ALU para soma 
            when "011" =>
                ALUCtl <= "0010"; 
		
	    -- 100: Para instrucoes vetoriais de soma e subtracao (ADD, ADDI e SUB)
	    -- A diferenca entre elas estara no funct3, assim como o tamanho dos vetores
	    when "100" => 
		ALUCtl <= "0011";

	    -- 101: Para o resto das instrucoes vetoriais (SLL, SRL, SLLI, SRLI)
	    -- A diferenca entre elas estara no funct3, assim como o tamanho dos vetores
	    when "101" => 
		ALUCtl <= "0111";
		
            -- Default
            when others =>
                ALUCtl <= "1111"; -- invalido
        end case;
    end process;
end Behavioral;
*/

/* Code of ForwardingUnit:
library IEEE;
use IEEE.STD_LOGIC_1164.ALL;
use IEEE.NUMERIC_STD.ALL;

entity ForwardingUnit is
    Port (
        ID_EX_RegisterRs1  : in  std_logic_vector(4 downto 0);
        ID_EX_RegisterRs2  : in  std_logic_vector(4 downto 0);

        EX_MEM_RegisterRd  : in  std_logic_vector(4 downto 0);
        EX_MEM_RegWrite    : in  std_logic;

        MEM_WB_RegisterRd  : in  std_logic_vector(4 downto 0);
        MEM_WB_RegWrite    : in  std_logic;

        ForwardA           : out std_logic_vector(1 downto 0);
        ForwardB           : out std_logic_vector(1 downto 0)
    );
end ForwardingUnit;

architecture Behavioral of ForwardingUnit is
begin
    process(ID_EX_RegisterRs1, ID_EX_RegisterRs2, EX_MEM_RegisterRd, EX_MEM_RegWrite,
            MEM_WB_RegisterRd, MEM_WB_RegWrite)
    begin
        -- forwardA, verifica se o rd escreve no registrador, se ele eh o x0 e se ele
				-- eh igual ao registrador source1 que ira ocorrer a execucao
				-- caso essas 3 condicoes sejam cumpridas eh enviado para o MUX de forwardA o sinal 10
				-- esse eh o EX HAZARD:
        if (EX_MEM_RegWrite = '1') and (EX_MEM_RegisterRd /= "00000") and
           (EX_MEM_RegisterRd = ID_EX_RegisterRs1) then
            ForwardA <= "10";
            
        -- esse eh o MEM HAZARD, tem que verificar se eh o foward mais recente, nao pode encaminhar
        -- do MEM se acabou de sair um novo valor do estagio EX.
        elsif (MEM_WB_RegWrite = '1') and (MEM_WB_RegisterRd /= "00000") and
              not (EX_MEM_RegWrite = '1' and EX_MEM_RegisterRd /= "00000" and
                   EX_MEM_RegisterRd = ID_EX_RegisterRs1) and
              (MEM_WB_RegisterRd = ID_EX_RegisterRs1) then
            ForwardA <= "01";
        else
            ForwardA <= "00";
        end if;

        -- mesma coisa que antes mas para o forwardB
        if (EX_MEM_RegWrite = '1') and (EX_MEM_RegisterRd /= "00000") and
           (EX_MEM_RegisterRd = ID_EX_RegisterRs2) then
            ForwardB <= "10";
            
        elsif (MEM_WB_RegWrite = '1') and (MEM_WB_RegisterRd /= "00000") and
              not (EX_MEM_RegWrite = '1' and EX_MEM_RegisterRd /= "00000" and
                   EX_MEM_RegisterRd = ID_EX_RegisterRs2) and
              (MEM_WB_RegisterRd = ID_EX_RegisterRs2) then
            ForwardB <= "01";
        else
            ForwardB <= "00";
        end if;
    end process;
end Behavioral;
*/

/* Code of ALUSrcA:
library IEEE;
use IEEE.STD_LOGIC_1164.ALL;

entity ALUSrcA is
    Port (
        Rs1  	: in  std_logic_vector(31 downto 0); -- Entrada de dados 0
        PC  	: in  std_logic_vector(31 downto 0); -- Entrada de dados 1
        SEL 	: in  std_logic_vector(1 downto 0); -- Linha de seleção de 2 bits
        A   	: out std_logic_vector(31 downto 0)  -- Saída de dados
    );
end ALUSrcA;

architecture Behavorial of ALUSrcA is
begin
    process(Rs1, PC, SEL)
    begin
        case SEL is
            when "00"   => A <= Rs1;
            when "01"   => A <= PC;
            when others => A <= (others => '0'); -- "10" e sinais incorretos
        end case;
    end process;

end Behavorial;
*/

/* Code of ALUSrcB:
library IEEE;
use IEEE.STD_LOGIC_1164.ALL;

entity ALUSrcB is
    Port (
        Rs2  	: in  std_logic_vector(31 downto 0); -- Entrada de dados 0
        imm  	: in  std_logic_vector(31 downto 0); -- Entrada de dados 1
        SEL 	: in  std_logic; -- Linha de seleção
        B   	: out std_logic_vector(31 downto 0)  -- Saída de dados
    );
end ALUSrcB;

architecture Behavorial of ALUSrcB is
begin
    process(Rs2, imm, SEL)
    begin
        case SEL is
            when '0'   => B <= Rs2;
            when others => B <= imm; -- '1'
        end case;
    end process;

end Behavorial;
*/

/* Code of ALU:
library IEEE;
use IEEE.STD_LOGIC_1164.ALL;
use IEEE.NUMERIC_STD.ALL;

entity ALU is
    Port (
        Funct3  : in  std_logic_vector(2 downto 0); -- para os malandros vetoriais
        ALUctl  : in  std_logic_vector(3 downto 0);
        A       : in  std_logic_vector(31 downto 0);
        B       : in  std_logic_vector(31 downto 0);
        ALUOut  : out std_logic_vector(31 downto 0)
    );
end ALU;

architecture Behavioral of ALU is
    signal result : std_logic_vector(31 downto 0);
begin

    process(ALUctl, Funct3, A, B)
        variable A_int         : signed(31 downto 0);
        variable B_int         : signed(31 downto 0);
        variable shift_amt     : integer;
        variable shift_res     : std_logic_vector(31 downto 0);
        variable B_signed      : std_logic_vector(31 downto 0);
        variable P_bits        : std_logic_vector(31 downto 0);
        variable G_bits        : std_logic_vector(31 downto 0);
        variable P_blocks      : std_logic_vector(7 downto 0);
        variable G_blocks      : std_logic_vector(7 downto 0);
        variable C_inter_block : std_logic_vector(8 downto 0);
        variable C0_for_block  : std_logic_vector(7 downto 0);
        variable C_bits        : std_logic_vector(32 downto 0);
        variable sum_sub_res   : std_logic_vector(31 downto 0);
    begin
        A_int := signed(A);
        B_int := signed(B);
        shift_amt := to_integer(unsigned(B(4 downto 0)));
        shift_res := (others => '0');

        case ALUctl is
            -- operacoes escalares
            when "0000" => result <= A and B;
            when "0001" => result <= A or B;
            when "0010" => result <= std_logic_vector(A_int + B_int);
            when "0110" => result <= std_logic_vector(A_int - B_int);
            when "1000" => result <= std_logic_vector(shift_left(unsigned(A), shift_amt));
            when "1001" => result <= std_logic_vector(shift_right(unsigned(A), shift_amt));
            when "1100" => result <= A xor B;

            -- operacoes de soma e subtracao vetorial integrada com a cpu sem simd AAAAAAAAAAAAAAAAAA
            when "0011" => -- sona ou subtracao vetorial
                if Funct3(2) = '1' then B_signed := not B; else B_signed := B; end if;
                P_bits := A xor B_signed;
                G_bits := A and B_signed;

                for i in 0 to 7 loop
                    P_blocks(i) := P_bits(i*4+3) and P_bits(i*4+2) and P_bits(i*4+1) and P_bits(i*4+0);
                    G_blocks(i) := G_bits(i*4+3) or (P_bits(i*4+3) and G_bits(i*4+2)) or (P_bits(i*4+3) and P_bits(i*4+2) and G_bits(i*4+1)) or (P_bits(i*4+3) and P_bits(i*4+2) and P_bits(i*4+1) and G_bits(i*4+0));
                end loop;

                C_inter_block(0) := Funct3(2);
                C_inter_block(1) := G_blocks(0) or (P_blocks(0) and C_inter_block(0));
                C_inter_block(2) := G_blocks(1) or (P_blocks(1) and G_blocks(0)) or (P_blocks(1) and P_blocks(0) and C_inter_block(0));
                C_inter_block(3) := G_blocks(2) or (P_blocks(2) and G_blocks(1)) or (P_blocks(2) and P_blocks(1) and G_blocks(0)) or (P_blocks(2) and P_blocks(1) and P_blocks(0) and C_inter_block(0));
                
                C_inter_block(4) := G_blocks(3) or (P_blocks(3) and G_blocks(2)) or (P_blocks(3) and P_blocks(2) and G_blocks(1)) or (P_blocks(3) and P_blocks(2) and P_blocks(1) and G_blocks(0)) or (P_blocks(3) and P_blocks(2) and P_blocks(1) and P_blocks(0) and C_inter_block(0));
                
                C_inter_block(5) := G_blocks(4) or (P_blocks(4) and C_inter_block(4));
                C_inter_block(6) := G_blocks(5) or (P_blocks(5) and G_blocks(4)) or (P_blocks(5) and P_blocks(4) and C_inter_block(4));
                C_inter_block(7) := G_blocks(6) or (P_blocks(6) and G_blocks(5)) or (P_blocks(6) and P_blocks(5) and G_blocks(4)) or (P_blocks(6) and P_blocks(5) and P_blocks(4) and C_inter_block(4));
                C_inter_block(8) := G_blocks(7) or (P_blocks(7) and G_blocks(6)) or (P_blocks(7) and P_blocks(6) and G_blocks(5)) or (P_blocks(7) and P_blocks(6) and P_blocks(5) and G_blocks(4)) or (P_blocks(7) and P_blocks(6) and P_blocks(5) and P_blocks(4) and C_inter_block(4));

                C0_for_block(0) := C_inter_block(0);
                C0_for_block(1) := (C_inter_block(1) and (Funct3(0) or Funct3(1))) or (Funct3(2) and (Funct3(0) nor Funct3(1)));
                C0_for_block(2) := (C_inter_block(2) and Funct3(1)) or (Funct3(2) and (not Funct3(1)));
                C0_for_block(3) := (C_inter_block(3) and (Funct3(0) or Funct3(1))) or (Funct3(2) and (Funct3(0) nor Funct3(1)));
                C0_for_block(4) := (C_inter_block(4) and Funct3(0) and Funct3(1)) or (Funct3(2) and (Funct3(0) nand Funct3(1)));
                C0_for_block(5) := (C_inter_block(5) and (Funct3(0) or Funct3(1))) or (Funct3(2) and (Funct3(0) nor Funct3(1)));
                C0_for_block(6) := (C_inter_block(6) and Funct3(1)) or (Funct3(2) and (not Funct3(1)));
                C0_for_block(7) := (C_inter_block(7) and (Funct3(0) or Funct3(1))) or (Funct3(2) and (Funct3(0) nor Funct3(1)));

                C_bits(0) := C0_for_block(0);
                for i in 0 to 7 loop
                    C_bits(i*4) := C0_for_block(i);
                    for j in 0 to 3 loop
                        sum_sub_res(i*4+j) := P_bits(i*4+j) xor C_bits(i*4+j);
                        C_bits(i*4+j+1)    := G_bits(i*4+j) or (P_bits(i*4+j) and C_bits(i*4+j));
                    end loop;
                end loop;
                result <= sum_sub_res;

            when "0111" => -- shift vetorial
			   -- a logica para shifts eh que o B tambem eh dividido em subvetores, dessa forma existe um deslocamento
		           -- especifico para cada subvetor de A 	
                if Funct3(2) = '0' then
                    case Funct3(1 downto 0) is
                        when "00" => for i in 0 to 7 loop shift_res(i*4+3 downto i*4) := std_logic_vector(shift_left(unsigned(A(i*4+3 downto i*4)), to_integer(unsigned(B(i*4+3 downto i*4))) )); end loop;
                        when "01" => for i in 0 to 3 loop shift_res(i*8+7 downto i*8) := std_logic_vector(shift_left(unsigned(A(i*8+7 downto i*8)), to_integer(unsigned(B(i*8+4 downto i*8))) )); end loop;
                        when "10" => for i in 0 to 1 loop shift_res(i*16+15 downto i*16) := std_logic_vector(shift_left(unsigned(A(i*16+15 downto i*16)), to_integer(unsigned(B(i*16+4 downto i*16))) )); end loop;
                        when "11" => shift_res := std_logic_vector(shift_left(unsigned(A), shift_amt));
                        when others => shift_res := (others => 'X');
                    end case;
                else
                    case Funct3(1 downto 0) is
                        when "00" => for i in 0 to 7 loop shift_res(i*4+3 downto i*4) := std_logic_vector(shift_right(unsigned(A(i*4+3 downto i*4)), to_integer(unsigned(B(i*4+3 downto i*4))) )); end loop;
                        when "01" => for i in 0 to 3 loop shift_res(i*8+7 downto i*8) := std_logic_vector(shift_right(unsigned(A(i*8+7 downto i*8)), to_integer(unsigned(B(i*8+4 downto i*8))) )); end loop;
                        when "10" => for i in 0 to 1 loop shift_res(i*16+15 downto i*16) := std_logic_vector(shift_right(unsigned(A(i*16+15 downto i*16)), to_integer(unsigned(B(i*16+4 downto i*16))) )); end loop;
                        when "11" => shift_res := std_logic_vector(shift_right(unsigned(A), shift_amt));
                        when others => shift_res := (others => 'X');
                    end case;
                end if;
                result <= shift_res;

            when others =>
                result <= (others => '0');
        end case;
    end process;

    ALUOut <= result;

end Behavioral;
*/

/* Code of EX_MEM:
library IEEE;
use IEEE.STD_LOGIC_1164.ALL;

entity EX_MEM is
    Port ( 
	rst     	: in  STD_LOGIC; 
        clk		: in  STD_LOGIC;

	ALUoutput_in	: in  STD_LOGIC_VECTOR(31 downto 0);
	rs2_data_in	: in  STD_LOGIC_VECTOR(31 downto 0); --for store instruction
        rd_in		: in  STD_LOGIC_VECTOR(4 downto 0);

	MEMSignals_in	: in STD_LOGIC_VECTOR(1 downto 0);
	WBSignals_in	: in STD_LOGIC_VECTOR(1 downto 0);

	ALUoutput_out	: out  STD_LOGIC_VECTOR(31 downto 0);
        rs2_data_out	: out STD_LOGIC_VECTOR(31 downto 0);
	MemRead		: out STD_LOGIC;
	MemWrite	: out STD_LOGIC;
	rd_out		: out STD_LOGIC_VECTOR(4 downto 0);
	WBSignals_out	: out STD_LOGIC_VECTOR(1 downto 0);
	RegWrite_out	: out STD_LOGIC
    );
end EX_MEM;

architecture Behavioral of EX_MEM is

signal s_dado : STD_LOGIC_VECTOR(31 downto 0);

begin

process(clk,rst)
begin
	if rst = '1' then
		rd_out <= (others => '0');
		rs2_data_out <= (others => '0');
		ALUoutput_out <= (others => '0');
		MemRead <= '0';
		MemWrite <= '0';
		WBSignals_out <= (others => '0');
		RegWrite_out <= '0';
        elsif rising_edge(clk) then
		rd_out <= rd_in;
		rs2_data_out <= rs2_data_in;
		ALUoutput_out <= ALUoutput_in;
		MemRead <= MEMSignals_in(0);
		MemWrite <= MEMSignals_in(1);
		WBSignals_out <= WBSignals_in;
		RegWrite_out <= WBSignals_in(1);
	end if;
end process;

end Behavioral;
*/

/* Code of RAM:
LIBRARY ieee;
USE ieee.std_logic_1164.all;
USE ieee.numeric_std.all;

entity RAM is
  port (
	clk: in std_logic;
	Dout: out std_logic_vector (31 downto 0);
	Addr: in std_logic_vector (31 downto 0);
	Din: in std_logic_vector (31 downto 0);
	Read: in std_logic;
	Write: in std_logic
	);
end RAM;

architecture Behavioral of RAM is
	type memoryType is array(0 to (2**16)-1) of STD_LOGIC_VECTOR(31 downto 0);
	signal memory : memoryType;
	signal A: std_logic_vector (15 downto 0);
begin

A <= Addr(15 downto 0);

process (clk)
begin
	if falling_edge(clk) then
		if Write='1' then
			memory(to_integer(unsigned(A))) <= Din;
		end if;
		if Read='1' then
			Dout <= memory(to_integer(unsigned(A)));
		else
			Dout <= (others => '0');
		end if;
	end if;
end process;

end Behavioral;
*/

/* Code of MEM_WB:
library IEEE;
use IEEE.STD_LOGIC_1164.ALL;

entity MEM_WB is
    Port ( 
	rst     	: in  STD_LOGIC; 
        clk		: in  STD_LOGIC;

        DataFromMem_in	: in  STD_LOGIC_VECTOR(31 downto 0);
	ALUoutput_in	: in  STD_LOGIC_VECTOR(31 downto 0);
        rd_in		: in  STD_LOGIC_VECTOR(4 downto 0);

	WBSignals_in	: in STD_LOGIC_VECTOR(1 downto 0);

	rd_out		: out STD_LOGIC_VECTOR(4 downto 0);
        DataFromMem_out	: out STD_LOGIC_VECTOR(31 downto 0);
	ALUoutput_out	: out  STD_LOGIC_VECTOR(31 downto 0);

	MemToReg 	: out STD_LOGIC;
	RegWrite 	: out STD_LOGIC
    );
end MEM_WB;

architecture Behavioral of MEM_WB is

signal s_dado : STD_LOGIC_VECTOR(31 downto 0);

begin

process(clk,rst)
begin
	if rst = '1' then
		rd_out <= (others => '0');
		DataFromMem_out <= (others => '0');
		ALUoutput_out <= (others => '0');
		MemToReg <= '0';
		RegWrite <= '0';
        elsif rising_edge(clk) then
		rd_out <= rd_in;
		DataFromMem_out <= DataFromMem_in;
		ALUoutput_out <= ALUoutput_in;
		MemToReg <= WBSignals_in(0);
		RegWrite <= WBSignals_in(1);
	end if;
end process;

end Behavioral;
*/

/* Code of MemToReg:
library IEEE;
use IEEE.STD_LOGIC_1164.ALL;

entity MemToReg is
    Port (
        MemOutput	: in  std_logic_vector(31 downto 0); -- Entrada de dados 0
        ALUOutput	: in  std_logic_vector(31 downto 0); -- Entrada de dados 1
        SEL		: in  std_logic; -- Linha de seleção
        DataOut		: out std_logic_vector(31 downto 0)  -- Saída de dados
    );
end MemToReg;

architecture Behavorial of MemToReg is
begin
    process(MemOutput, ALUOutput, SEL)
    begin
        case SEL is
            when '1'   => DataOut <= MemOutput;
            when '0'   => DataOut <= ALUOutput;
            when others => DataOut <= (others => '0'); -- Cobre o caso "11" e outros possíveis (U, X, etc.)
        end case;
    end process;

end Behavorial;
*/
